// Logisim project 206722894_fsm.circ as structural Verilog: 2 circuits, main circuit fsm
module fsm (
  input  p,
  input  m,
  input  CLK,
  output d,
  output [3:0] c
);

  wire and_1_out, and_2_out, and_3_out, and_4_out, and_5_out, and_6_out, and_7_out, and_8_out, and_9_out,
       and_10_out, and_11_out, and_12_out, and_13_out, and_14_out, and_15_out, and_16_out, and_17_out,
       and_18_out, and_19_out, and_20_out, and_21_out, and_22_out, and_23_out, and_24_out, and_25_out,
       and_26_out, and_27_out, and_28_out, and_29_out, and_30_out, and_31_out, and_32_out,
       debugger_1_product_delivered, debugger_1_product_selected, not_1_out, not_2_out, not_3_out, not_4_out,
       not_5_out, not_6_out, not_7_out, not_8_out, not_9_out, not_10_out, not_11_out, not_12_out, not_13_out,
       not_14_out, not_15_out, not_16_out, not_17_out, or_1_out, or_2_out, or_3_out, or_5_out, or_6_out,
       or_7_out, or_8_out, or_10_out, or_13_out, or_14_out;
  wire [1:0] NS;
  wire [3:0] debugger_1_change_returned, debugger_1_money_inserted, debugger_1_next_state__q_0_q_5_q_10,
       debugger_1_state__q_0_q_5_q_10;

  not not_1 (not_1_out, NS[1]);
  not not_2 (not_2_out, NS[0]);
  not not_3 (not_3_out, p);
  not not_4 (not_4_out, p);
  not not_5 (not_5_out, NS[1]);
  not not_6 (not_6_out, NS[0]);
  not not_7 (not_7_out, p);
  not not_8 (not_8_out, m);
  and and_1 (and_1_out, NS[0], m);
  and and_2 (and_2_out, NS[0], p);
  not not_9 (not_9_out, NS[0]);
  not not_10 (not_10_out, m);
  not not_11 (not_11_out, NS[0]);
  not not_12 (not_12_out, p);
  and and_3 (and_3_out, not_1_out, not_2_out);
  and and_4 (and_4_out, not_3_out, m);
  and and_5 (and_5_out, NS[0], not_4_out);
  not not_13 (not_13_out, m);
  and and_6 (and_6_out, not_5_out, not_6_out);
  and and_7 (and_7_out, not_7_out, not_8_out);
  or or_1 (or_1_out, p, and_1_out);
  and and_8 (and_8_out, and_2_out, m);
  and and_9 (and_9_out, NS[1], m);
  and and_10 (and_10_out, NS[1], p);
  and and_11 (and_11_out, NS[1], NS[0]);
  and and_12 (and_12_out, not_9_out, p);
  and and_13 (and_13_out, NS[0], p);
  not not_14 (not_14_out, m);
  and and_14 (and_14_out, NS[0], m);
  and and_15 (and_15_out, NS[1], not_10_out);
  and and_16 (and_16_out, not_11_out, p);
  and and_17 (and_17_out, NS[0], not_12_out);
  not not_15 (not_15_out, p);
  and and_18 (and_18_out, and_3_out, and_4_out);
  or or_2 (or_2_out, and_18_out, and_19_out);
  and and_19 (and_19_out, and_5_out, not_13_out);
  and and_20 (and_20_out, and_6_out, and_7_out);
  or or_3 (or_3_out, and_20_out, and_21_out);
  and and_21 (and_21_out, NS[1], NS[0]);
  or or_4 (d, or_1_out, NS[1]);
  or or_5 (or_5_out, and_8_out, and_9_out);
  or or_6 (or_6_out, and_10_out, and_11_out);
  and and_22 (and_22_out, and_12_out, m);
  or or_7 (or_7_out, and_22_out, and_23_out);
  and and_23 (and_23_out, and_13_out, not_14_out);
  and and_24 (and_24_out, NS[1], NS[0]);
  or or_8 (or_8_out, and_14_out, and_15_out);
  or or_9 (c[1], or_8_out, and_25_out);
  and and_25 (and_25_out, NS[1], p);
  and and_26 (and_26_out, and_16_out, m);
  or or_10 (or_10_out, and_26_out, and_27_out);
  and and_27 (and_27_out, and_17_out, m);
  and and_28 (and_28_out, NS[0], p);
  and and_29 (and_29_out, and_28_out, not_16_out);
  not not_16 (not_16_out, m);
  and and_30 (and_30_out, NS[1], not_15_out);
  and and_31 (and_31_out, and_30_out, not_17_out);
  not not_17 (not_17_out, m);
  and and_32 (and_32_out, NS[1], NS[0]);
  or or_11 (c[3], or_5_out, or_6_out);
  or or_12 (c[2], or_7_out, and_24_out);
  or or_13 (or_13_out, or_10_out, and_29_out);
  or or_14 (or_14_out, and_31_out, and_32_out);
  D_Flip_Flop d_ff_1 (.clk(CLK), .D(or_2_out), .Q(NS[1]));  // open: Qn, preset, en, reset
  D_Flip_Flop d_ff_2 (.clk(CLK), .D(or_3_out), .Q(NS[0]));  // open: Qn, preset, en, reset
  or or_15 (c[0], or_13_out, or_14_out);
  debugger debugger_1 (
    .S(NS), .p(p), .m(m), .NS(NS), .d(d), .c(c), .state__q_0_q_5_q_10(debugger_1_state__q_0_q_5_q_10),
    .product_selected(debugger_1_product_selected), .money_inserted(debugger_1_money_inserted),
    .next_state__q_0_q_5_q_10(debugger_1_next_state__q_0_q_5_q_10),
    .product_delivered(debugger_1_product_delivered), .change_returned(debugger_1_change_returned));
  // Probe on debugger_1_state__q_0_q_5_q_10
  // Probe on debugger_1_product_selected
  // Probe on debugger_1_money_inserted
  // Probe on debugger_1_next_state__q_0_q_5_q_10
  // Probe on debugger_1_product_delivered
  // Probe on debugger_1_change_returned

  // Other names for the same wires on the sheet: S[1:0] = NS; S0 = NS[0]; S1 = NS[1]
endmodule

module debugger (
  input  [1:0] S,
  input  p,
  input  m,
  input  [1:0] NS,
  input  d,
  input  [3:0] c,
  output [3:0] state__q_0_q_5_q_10,
  output product_selected,
  output [3:0] money_inserted,
  output [3:0] next_state__q_0_q_5_q_10,
  output product_delivered,
  output [3:0] change_returned
);

  Multiplexer #(.width(4), .enable("false")) multiplexer_1 (
    .in0(4'b0101), .in1(4'b1010), .out(money_inserted), .sel(m));
  Multiplexer #(.select(2), .width(4), .enable("false")) multiplexer_2 (
    .in0(4'b0000), .in1(4'b0101), .in2(4'b1010), .out(state__q_0_q_5_q_10), .sel(S));  // open: in3
  Multiplexer #(.select(2), .width(4), .enable("false")) multiplexer_3 (
    .in0(4'b0000), .in1(4'b0101), .in2(4'b1010), .out(next_state__q_0_q_5_q_10), .sel(NS));  // open: in3

  assign change_returned = c;
  assign product_delivered = d;
  assign product_selected = p;
endmodule
