// Logisim project 206722894_matmul.circ as structural Verilog: 11 circuits, main circuit matmul
module matmul (
  input  [7:0] x_row_0,
  input  [7:0] x_row_1,
  input  [7:0] x_row_2,
  input  [7:0] x_row_3,
  input  [7:0] x_row_4,
  input  [7:0] x_row_5,
  input  [7:0] x_row_6,
  input  [7:0] x_row_7,
  input  [7:0] y_row_0,
  input  [7:0] y_row_1,
  input  [7:0] y_row_2,
  input  [7:0] y_row_3,
  input  [7:0] y_row_4,
  input  [7:0] y_row_5,
  input  [7:0] y_row_6,
  input  [7:0] y_row_7,
  output [7:0] z_row_0,
  output [7:0] z_row_1,
  output [7:0] z_row_2,
  output [7:0] z_row_3,
  output [7:0] z_row_4,
  output [7:0] z_row_5,
  output [7:0] z_row_6,
  output [7:0] z_row_7
);

  wire [7:0] y_col_0, y_col_1, y_col_2, y_col_3, y_col_4, y_col_5, y_col_6, y_col_7;

  matmul_step_2 matmul_step_2_1 (
    .row(x_row_0), .col_0(y_col_0), .col_1(y_col_1), .col_2(y_col_2), .col_3(y_col_3), .col_4(y_col_4),
    .col_5(y_col_5), .col_6(y_col_6), .col_7(y_col_7), .product_row(z_row_0));
  matmul_step_2 matmul_step_2_2 (
    .row(x_row_1), .col_0(y_col_0), .col_1(y_col_1), .col_2(y_col_2), .col_3(y_col_3), .col_4(y_col_4),
    .col_5(y_col_5), .col_6(y_col_6), .col_7(y_col_7), .product_row(z_row_1));
  matmul_step_2 matmul_step_2_3 (
    .row(x_row_2), .col_0(y_col_0), .col_1(y_col_1), .col_2(y_col_2), .col_3(y_col_3), .col_4(y_col_4),
    .col_5(y_col_5), .col_6(y_col_6), .col_7(y_col_7), .product_row(z_row_2));
  DotMatrix #(.inputtype("row"), .matrixcols(8), .matrixrows(8)) dotmatrix_1 (
    .row0(x_row_0), .row1(x_row_1), .row2(x_row_2), .row3(x_row_3), .row4(x_row_4), .row5(x_row_5),
    .row6(x_row_6), .row7(x_row_7));
  DotMatrix #(.inputtype("row"), .matrixcols(8), .matrixrows(8)) dotmatrix_2 (
    .row0(y_row_0), .row1(y_row_1), .row2(y_row_2), .row3(y_row_3), .row4(y_row_4), .row5(y_row_5),
    .row6(y_row_6), .row7(y_row_7));
  matmul_step_2 matmul_step_2_4 (
    .row(x_row_3), .col_0(y_col_0), .col_1(y_col_1), .col_2(y_col_2), .col_3(y_col_3), .col_4(y_col_4),
    .col_5(y_col_5), .col_6(y_col_6), .col_7(y_col_7), .product_row(z_row_3));
  matmul_step_2 matmul_step_2_5 (
    .row(x_row_4), .col_0(y_col_0), .col_1(y_col_1), .col_2(y_col_2), .col_3(y_col_3), .col_4(y_col_4),
    .col_5(y_col_5), .col_6(y_col_6), .col_7(y_col_7), .product_row(z_row_4));
  matmul_step_2 matmul_step_2_6 (
    .row(x_row_5), .col_0(y_col_0), .col_1(y_col_1), .col_2(y_col_2), .col_3(y_col_3), .col_4(y_col_4),
    .col_5(y_col_5), .col_6(y_col_6), .col_7(y_col_7), .product_row(z_row_5));
  DotMatrix #(.inputtype("row"), .matrixcols(8), .matrixrows(8)) dotmatrix_3 (
    .row0(y_col_0), .row1(y_col_1), .row2(y_col_2), .row3(y_col_3), .row4(y_col_4), .row5(y_col_5),
    .row6(y_col_6), .row7(y_col_7));
  DotMatrix #(.inputtype("row"), .matrixcols(8), .matrixrows(8)) dotmatrix_4 (
    .row0(z_row_0), .row1(z_row_1), .row2(z_row_2), .row3(z_row_3), .row4(z_row_4), .row5(z_row_5),
    .row6(z_row_6), .row7(z_row_7));
  matmul_step_2 matmul_step_2_7 (
    .row(x_row_6), .col_0(y_col_0), .col_1(y_col_1), .col_2(y_col_2), .col_3(y_col_3), .col_4(y_col_4),
    .col_5(y_col_5), .col_6(y_col_6), .col_7(y_col_7), .product_row(z_row_6));
  matmul_step_2 matmul_step_2_8 (
    .row(x_row_7), .col_0(y_col_0), .col_1(y_col_1), .col_2(y_col_2), .col_3(y_col_3), .col_4(y_col_4),
    .col_5(y_col_5), .col_6(y_col_6), .col_7(y_col_7), .product_row(z_row_7));
  transpose transpose_1 (
    .row_0(y_row_0), .row_1(y_row_1), .row_2(y_row_2), .row_3(y_row_3), .row_4(y_row_4), .row_5(y_row_5),
    .row_6(y_row_6), .row_7(y_row_7), .column_0(y_col_0), .column_1(y_col_1), .column_2(y_col_2),
    .column_3(y_col_3), .column_4(y_col_4), .column_5(y_col_5), .column_6(y_col_6), .column_7(y_col_7));
endmodule

module transpose (
  input  [7:0] row_0,
  input  [7:0] row_1,
  input  [7:0] row_2,
  input  [7:0] row_3,
  input  [7:0] row_4,
  input  [7:0] row_5,
  input  [7:0] row_6,
  input  [7:0] row_7,
  output [7:0] column_0,
  output [7:0] column_1,
  output [7:0] column_2,
  output [7:0] column_3,
  output [7:0] column_4,
  output [7:0] column_5,
  output [7:0] column_6,
  output [7:0] column_7
);

  extract_col extract_col_1 (
    .in_1(3'b000), .row_0(row_0), .row_1(row_1), .row_2(row_2), .row_3(row_3), .row_4(row_4), .row_5(row_5),
    .row_6(row_6), .row_7(row_7), .b(column_0));
  extract_col extract_col_2 (
    .in_1(3'b100), .row_0(row_0), .row_1(row_1), .row_2(row_2), .row_3(row_3), .row_4(row_4), .row_5(row_5),
    .row_6(row_6), .row_7(row_7), .b(column_4));
  extract_col extract_col_3 (
    .in_1(3'b001), .row_0(row_0), .row_1(row_1), .row_2(row_2), .row_3(row_3), .row_4(row_4), .row_5(row_5),
    .row_6(row_6), .row_7(row_7), .b(column_1));
  extract_col extract_col_4 (
    .in_1(3'b101), .row_0(row_0), .row_1(row_1), .row_2(row_2), .row_3(row_3), .row_4(row_4), .row_5(row_5),
    .row_6(row_6), .row_7(row_7), .b(column_5));
  extract_col extract_col_5 (
    .in_1(3'b010), .row_0(row_0), .row_1(row_1), .row_2(row_2), .row_3(row_3), .row_4(row_4), .row_5(row_5),
    .row_6(row_6), .row_7(row_7), .b(column_2));
  extract_col extract_col_6 (
    .in_1(3'b110), .row_0(row_0), .row_1(row_1), .row_2(row_2), .row_3(row_3), .row_4(row_4), .row_5(row_5),
    .row_6(row_6), .row_7(row_7), .b(column_6));
  extract_col extract_col_7 (
    .in_1(3'b011), .row_0(row_0), .row_1(row_1), .row_2(row_2), .row_3(row_3), .row_4(row_4), .row_5(row_5),
    .row_6(row_6), .row_7(row_7), .b(column_3));
  extract_col extract_col_8 (
    .in_1(3'b111), .row_0(row_0), .row_1(row_1), .row_2(row_2), .row_3(row_3), .row_4(row_4), .row_5(row_5),
    .row_6(row_6), .row_7(row_7), .b(column_7));
endmodule

module extract_col (
  input  [2:0] in_1,
  input  [7:0] row_0,
  input  [7:0] row_1,
  input  [7:0] row_2,
  input  [7:0] row_3,
  input  [7:0] row_4,
  input  [7:0] row_5,
  input  [7:0] row_6,
  input  [7:0] row_7,
  output [7:0] b
);

  wire [2:0] not_1_out, not_2_out, not_3_out, not_4_out, not_5_out, not_6_out, not_7_out, not_8_out;

  BitSelector bitselector_1 (.in(row_0), .out(b[7]), .sel(not_1_out));
  assign not_1_out = ~in_1;  // NOT_Gate not_1, 3 bits wide
  BitSelector bitselector_2 (.in(row_1), .out(b[6]), .sel(not_2_out));
  assign not_2_out = ~in_1;  // NOT_Gate not_2, 3 bits wide
  BitSelector bitselector_3 (.in(row_2), .out(b[5]), .sel(not_3_out));
  assign not_3_out = ~in_1;  // NOT_Gate not_3, 3 bits wide
  BitSelector bitselector_4 (.in(row_3), .out(b[4]), .sel(not_4_out));
  assign not_4_out = ~in_1;  // NOT_Gate not_4, 3 bits wide
  BitSelector bitselector_5 (.in(row_4), .out(b[3]), .sel(not_5_out));
  assign not_5_out = ~in_1;  // NOT_Gate not_5, 3 bits wide
  BitSelector bitselector_6 (.in(row_5), .out(b[2]), .sel(not_6_out));
  assign not_6_out = ~in_1;  // NOT_Gate not_6, 3 bits wide
  BitSelector bitselector_7 (.in(row_6), .out(b[1]), .sel(not_7_out));
  assign not_7_out = ~in_1;  // NOT_Gate not_7, 3 bits wide
  BitSelector bitselector_8 (.in(row_7), .out(b[0]), .sel(not_8_out));
  assign not_8_out = ~in_1;  // NOT_Gate not_8, 3 bits wide

  // Other names for the same wires on the sheet: col[7:0] = b; col_num[2:0] = in_1
endmodule

module matmul_step_1 (
  input  [7:0] row,
  input  [7:0] col,
  output \output 
);

  wire and_1_out, and_2_out, and_3_out, and_4_out, and_5_out, and_6_out, and_7_out, and_8_out, or_1_out,
       or_2_out, or_3_out, or_4_out, or_5_out, or_6_out;

  and and_1 (and_1_out, row[0], col[0]);
  and and_2 (and_2_out, row[1], col[1]);
  and and_3 (and_3_out, row[2], col[2]);
  and and_4 (and_4_out, row[3], col[3]);
  and and_5 (and_5_out, row[4], col[4]);
  and and_6 (and_6_out, row[5], col[5]);
  and and_7 (and_7_out, row[6], col[6]);
  and and_8 (and_8_out, row[7], col[7]);
  or or_1 (or_1_out, and_1_out, and_2_out);
  or or_2 (or_2_out, and_3_out, and_4_out);
  or or_3 (or_3_out, and_5_out, and_6_out);
  or or_4 (or_4_out, and_7_out, and_8_out);
  or or_5 (or_5_out, or_1_out, or_2_out);
  or or_6 (or_6_out, or_3_out, or_4_out);
  or or_7 (\output , or_5_out, or_6_out);

  // Other names for the same wires on the sheet: col_0 = col[0]; col_1 = col[1]; col_2 = col[2]; col_3 = col[3];
  //   col_4 = col[4]; col_5 = col[5]; col_6 = col[6]; col_7 = col[7]; row_0 = row[0]; row_1 = row[1]; row_2 = row[2];
  //   row_3 = row[3]; row_4 = row[4]; row_5 = row[5]; row_6 = row[6]; row_7 = row[7]
endmodule

module matmul_step_2 (
  input  [7:0] row,
  input  [7:0] col_0,
  input  [7:0] col_1,
  input  [7:0] col_2,
  input  [7:0] col_3,
  input  [7:0] col_4,
  input  [7:0] col_5,
  input  [7:0] col_6,
  input  [7:0] col_7,
  output [7:0] product_row
);

  matmul_step_1 matmul_step_1_1 (.row(row), .col(col_0), .\output (product_row[7]));
  matmul_step_1 matmul_step_1_2 (.row(row), .col(col_1), .\output (product_row[6]));
  matmul_step_1 matmul_step_1_3 (.row(row), .col(col_2), .\output (product_row[5]));
  matmul_step_1 matmul_step_1_4 (.row(row), .col(col_3), .\output (product_row[4]));
  matmul_step_1 matmul_step_1_5 (.row(row), .col(col_4), .\output (product_row[3]));
  matmul_step_1 matmul_step_1_6 (.row(row), .col(col_5), .\output (product_row[2]));
  matmul_step_1 matmul_step_1_7 (.row(row), .col(col_6), .\output (product_row[1]));
  matmul_step_1 matmul_step_1_8 (.row(row), .col(col_7), .\output (product_row[0]));
endmodule

// OR
module bitwise_or_8_8 (
  input  [7:0] x_row_0,
  input  [7:0] x_row_1,
  input  [7:0] x_row_2,
  input  [7:0] x_row_3,
  input  [7:0] x_row_4,
  input  [7:0] x_row_5,
  input  [7:0] x_row_6,
  input  [7:0] x_row_7,
  input  [7:0] y_row_0,
  input  [7:0] y_row_1,
  input  [7:0] y_row_2,
  input  [7:0] y_row_3,
  input  [7:0] y_row_4,
  input  [7:0] y_row_5,
  input  [7:0] y_row_6,
  input  [7:0] y_row_7,
  output [7:0] z_row_0,
  output [7:0] z_row_1,
  output [7:0] z_row_2,
  output [7:0] z_row_3,
  output [7:0] z_row_4,
  output [7:0] z_row_5,
  output [7:0] z_row_6,
  output [7:0] z_row_7
);

  assign z_row_0 = x_row_0 | y_row_0;  // OR_Gate or_1, 8 bits wide
  assign z_row_1 = x_row_1 | y_row_1;  // OR_Gate or_2, 8 bits wide
  assign z_row_2 = x_row_2 | y_row_2;  // OR_Gate or_3, 8 bits wide
  assign z_row_3 = x_row_3 | y_row_3;  // OR_Gate or_4, 8 bits wide
  assign z_row_4 = x_row_4 | y_row_4;  // OR_Gate or_5, 8 bits wide
  assign z_row_5 = x_row_5 | y_row_5;  // OR_Gate or_6, 8 bits wide
  assign z_row_6 = x_row_6 | y_row_6;  // OR_Gate or_7, 8 bits wide
  assign z_row_7 = x_row_7 | y_row_7;  // OR_Gate or_8, 8 bits wide
  DotMatrix #(.inputtype("row"), .matrixcols(8), .matrixrows(8)) dotmatrix_1 (
    .row0(x_row_0), .row1(x_row_1), .row2(x_row_2), .row3(x_row_3), .row4(x_row_4), .row5(x_row_5),
    .row6(x_row_6), .row7(x_row_7));
  DotMatrix #(.inputtype("row"), .matrixcols(8), .matrixrows(8)) dotmatrix_2 (
    .row0(y_row_0), .row1(y_row_1), .row2(y_row_2), .row3(y_row_3), .row4(y_row_4), .row5(y_row_5),
    .row6(y_row_6), .row7(y_row_7));
  DotMatrix #(.inputtype("row"), .matrixcols(8), .matrixrows(8)) dotmatrix_3 (
    .row0(z_row_0), .row1(z_row_1), .row2(z_row_2), .row3(z_row_3), .row4(z_row_4), .row5(z_row_5),
    .row6(z_row_6), .row7(z_row_7));
endmodule

module is_connected (
  input  [7:0] x_row_0,
  input  [7:0] x_row_1,
  input  [7:0] x_row_2,
  input  [7:0] x_row_3,
  input  [7:0] x_row_4,
  input  [7:0] x_row_5,
  input  [7:0] x_row_6,
  input  [7:0] x_row_7,
  output is_connected
);

  wire [7:0] bitwise_or_8_8_1_z_row_0, bitwise_or_8_8_1_z_row_1, bitwise_or_8_8_1_z_row_2,
       bitwise_or_8_8_1_z_row_3, bitwise_or_8_8_1_z_row_4, bitwise_or_8_8_1_z_row_5,
       bitwise_or_8_8_1_z_row_6, bitwise_or_8_8_1_z_row_7, bitwise_or_8_8_2_z_row_0,
       bitwise_or_8_8_2_z_row_1, bitwise_or_8_8_2_z_row_2, bitwise_or_8_8_2_z_row_3,
       bitwise_or_8_8_2_z_row_4, bitwise_or_8_8_2_z_row_5, bitwise_or_8_8_2_z_row_6,
       bitwise_or_8_8_2_z_row_7, bitwise_or_8_8_3_z_row_0, bitwise_or_8_8_3_z_row_1,
       bitwise_or_8_8_3_z_row_2, bitwise_or_8_8_3_z_row_3, bitwise_or_8_8_3_z_row_4,
       bitwise_or_8_8_3_z_row_5, bitwise_or_8_8_3_z_row_6, bitwise_or_8_8_3_z_row_7,
       bitwise_or_8_8_4_z_row_0, bitwise_or_8_8_4_z_row_1, bitwise_or_8_8_4_z_row_2,
       bitwise_or_8_8_4_z_row_3, bitwise_or_8_8_4_z_row_4, bitwise_or_8_8_4_z_row_5,
       bitwise_or_8_8_4_z_row_6, bitwise_or_8_8_4_z_row_7, bitwise_or_8_8_5_z_row_0,
       bitwise_or_8_8_5_z_row_1, bitwise_or_8_8_5_z_row_2, bitwise_or_8_8_5_z_row_3,
       bitwise_or_8_8_5_z_row_4, bitwise_or_8_8_5_z_row_5, bitwise_or_8_8_5_z_row_6,
       bitwise_or_8_8_5_z_row_7, bitwise_or_8_8_6_z_row_0, bitwise_or_8_8_6_z_row_1,
       bitwise_or_8_8_6_z_row_2, bitwise_or_8_8_6_z_row_3, bitwise_or_8_8_6_z_row_4,
       bitwise_or_8_8_6_z_row_5, bitwise_or_8_8_6_z_row_6, bitwise_or_8_8_6_z_row_7,
       bitwise_or_8_8_7_z_row_0, bitwise_or_8_8_7_z_row_1, bitwise_or_8_8_7_z_row_2,
       bitwise_or_8_8_7_z_row_3, bitwise_or_8_8_7_z_row_4, bitwise_or_8_8_7_z_row_5,
       bitwise_or_8_8_7_z_row_6, bitwise_or_8_8_7_z_row_7, x2_row_0, x2_row_1, x2_row_2, x2_row_3, x2_row_4,
       x2_row_5, x2_row_6, x2_row_7, x3_row_0, x3_row_1, x3_row_2, x3_row_3, x3_row_4, x3_row_5, x3_row_6,
       x3_row_7, x4_row_0, x4_row_1, x4_row_2, x4_row_3, x4_row_4, x4_row_5, x4_row_6, x4_row_7, x5_row_0,
       x5_row_1, x5_row_2, x5_row_3, x5_row_4, x5_row_5, x5_row_6, x5_row_7, x6_row_0, x6_row_1, x6_row_2,
       x6_row_3, x6_row_4, x6_row_5, x6_row_6, x6_row_7, x7_row_0, x7_row_1, x7_row_2, x7_row_3, x7_row_4,
       x7_row_5, x7_row_6, x7_row_7;

  matmul matmul_1 (
    .x_row_0(x_row_0), .x_row_1(x_row_1), .x_row_2(x_row_2), .x_row_3(x_row_3), .x_row_4(x_row_4),
    .x_row_5(x_row_5), .x_row_6(x_row_6), .x_row_7(x_row_7), .y_row_0(x_row_0), .y_row_1(x_row_1),
    .y_row_2(x_row_2), .y_row_3(x_row_3), .y_row_4(x_row_4), .y_row_5(x_row_5), .y_row_6(x_row_6),
    .y_row_7(x_row_7), .z_row_0(x2_row_0), .z_row_1(x2_row_1), .z_row_2(x2_row_2), .z_row_3(x2_row_3),
    .z_row_4(x2_row_4), .z_row_5(x2_row_5), .z_row_6(x2_row_6), .z_row_7(x2_row_7));
  matmul matmul_2 (
    .x_row_0(x2_row_0), .x_row_1(x2_row_1), .x_row_2(x2_row_2), .x_row_3(x2_row_3), .x_row_4(x2_row_4),
    .x_row_5(x2_row_5), .x_row_6(x2_row_6), .x_row_7(x2_row_7), .y_row_0(x_row_0), .y_row_1(x_row_1),
    .y_row_2(x_row_2), .y_row_3(x_row_3), .y_row_4(x_row_4), .y_row_5(x_row_5), .y_row_6(x_row_6),
    .y_row_7(x_row_7), .z_row_0(x3_row_0), .z_row_1(x3_row_1), .z_row_2(x3_row_2), .z_row_3(x3_row_3),
    .z_row_4(x3_row_4), .z_row_5(x3_row_5), .z_row_6(x3_row_6), .z_row_7(x3_row_7));
  matmul matmul_3 (
    .x_row_0(x3_row_0), .x_row_1(x3_row_1), .x_row_2(x3_row_2), .x_row_3(x3_row_3), .x_row_4(x3_row_4),
    .x_row_5(x3_row_5), .x_row_6(x3_row_6), .x_row_7(x3_row_7), .y_row_0(x_row_0), .y_row_1(x_row_1),
    .y_row_2(x_row_2), .y_row_3(x_row_3), .y_row_4(x_row_4), .y_row_5(x_row_5), .y_row_6(x_row_6),
    .y_row_7(x_row_7), .z_row_0(x4_row_0), .z_row_1(x4_row_1), .z_row_2(x4_row_2), .z_row_3(x4_row_3),
    .z_row_4(x4_row_4), .z_row_5(x4_row_5), .z_row_6(x4_row_6), .z_row_7(x4_row_7));
  DotMatrix #(.inputtype("row"), .matrixcols(8), .matrixrows(8)) dotmatrix_1 (
    .row0(x_row_0), .row1(x_row_1), .row2(x_row_2), .row3(x_row_3), .row4(x_row_4), .row5(x_row_5),
    .row6(x_row_6), .row7(x_row_7));
  matmul matmul_4 (
    .x_row_0(x4_row_0), .x_row_1(x4_row_1), .x_row_2(x4_row_2), .x_row_3(x4_row_3), .x_row_4(x4_row_4),
    .x_row_5(x4_row_5), .x_row_6(x4_row_6), .x_row_7(x4_row_7), .y_row_0(x_row_0), .y_row_1(x_row_1),
    .y_row_2(x_row_2), .y_row_3(x_row_3), .y_row_4(x_row_4), .y_row_5(x_row_5), .y_row_6(x_row_6),
    .y_row_7(x_row_7), .z_row_0(x5_row_0), .z_row_1(x5_row_1), .z_row_2(x5_row_2), .z_row_3(x5_row_3),
    .z_row_4(x5_row_4), .z_row_5(x5_row_5), .z_row_6(x5_row_6), .z_row_7(x5_row_7));
  matmul matmul_5 (
    .x_row_0(x5_row_0), .x_row_1(x5_row_1), .x_row_2(x5_row_2), .x_row_3(x5_row_3), .x_row_4(x5_row_4),
    .x_row_5(x5_row_5), .x_row_6(x5_row_6), .x_row_7(x5_row_7), .y_row_0(x_row_0), .y_row_1(x_row_1),
    .y_row_2(x_row_2), .y_row_3(x_row_3), .y_row_4(x_row_4), .y_row_5(x_row_5), .y_row_6(x_row_6),
    .y_row_7(x_row_7), .z_row_0(x6_row_0), .z_row_1(x6_row_1), .z_row_2(x6_row_2), .z_row_3(x6_row_3),
    .z_row_4(x6_row_4), .z_row_5(x6_row_5), .z_row_6(x6_row_6), .z_row_7(x6_row_7));
  matmul matmul_6 (
    .x_row_0(x6_row_0), .x_row_1(x6_row_1), .x_row_2(x6_row_2), .x_row_3(x6_row_3), .x_row_4(x6_row_4),
    .x_row_5(x6_row_5), .x_row_6(x6_row_6), .x_row_7(x6_row_7), .y_row_0(x_row_0), .y_row_1(x_row_1),
    .y_row_2(x_row_2), .y_row_3(x_row_3), .y_row_4(x_row_4), .y_row_5(x_row_5), .y_row_6(x_row_6),
    .y_row_7(x_row_7), .z_row_0(x7_row_0), .z_row_1(x7_row_1), .z_row_2(x7_row_2), .z_row_3(x7_row_3),
    .z_row_4(x7_row_4), .z_row_5(x7_row_5), .z_row_6(x7_row_6), .z_row_7(x7_row_7));
  bitwise_or_8_8 bitwise_or_8_8_1 (
    .x_row_0(x_row_0), .x_row_1(x_row_1), .x_row_2(x_row_2), .x_row_3(x_row_3), .x_row_4(x_row_4),
    .x_row_5(x_row_5), .x_row_6(x_row_6), .x_row_7(x_row_7), .y_row_0(x2_row_0), .y_row_1(x2_row_1),
    .y_row_2(x2_row_2), .y_row_3(x2_row_3), .y_row_4(x2_row_4), .y_row_5(x2_row_5), .y_row_6(x2_row_6),
    .y_row_7(x2_row_7), .z_row_0(bitwise_or_8_8_1_z_row_0), .z_row_1(bitwise_or_8_8_1_z_row_1),
    .z_row_2(bitwise_or_8_8_1_z_row_2), .z_row_3(bitwise_or_8_8_1_z_row_3),
    .z_row_4(bitwise_or_8_8_1_z_row_4), .z_row_5(bitwise_or_8_8_1_z_row_5),
    .z_row_6(bitwise_or_8_8_1_z_row_6), .z_row_7(bitwise_or_8_8_1_z_row_7));
  bitwise_or_8_8 bitwise_or_8_8_2 (
    .x_row_0(bitwise_or_8_8_1_z_row_0), .x_row_1(bitwise_or_8_8_1_z_row_1),
    .x_row_2(bitwise_or_8_8_1_z_row_2), .x_row_3(bitwise_or_8_8_1_z_row_3),
    .x_row_4(bitwise_or_8_8_1_z_row_4), .x_row_5(bitwise_or_8_8_1_z_row_5),
    .x_row_6(bitwise_or_8_8_1_z_row_6), .x_row_7(bitwise_or_8_8_1_z_row_7), .y_row_0(x3_row_0),
    .y_row_1(x3_row_1), .y_row_2(x3_row_2), .y_row_3(x3_row_3), .y_row_4(x3_row_4), .y_row_5(x3_row_5),
    .y_row_6(x3_row_6), .y_row_7(x3_row_7), .z_row_0(bitwise_or_8_8_2_z_row_0),
    .z_row_1(bitwise_or_8_8_2_z_row_1), .z_row_2(bitwise_or_8_8_2_z_row_2),
    .z_row_3(bitwise_or_8_8_2_z_row_3), .z_row_4(bitwise_or_8_8_2_z_row_4),
    .z_row_5(bitwise_or_8_8_2_z_row_5), .z_row_6(bitwise_or_8_8_2_z_row_6), .z_row_7(bitwise_or_8_8_2_z_row_7));
  bitwise_or_8_8 bitwise_or_8_8_3 (
    .x_row_0(bitwise_or_8_8_2_z_row_0), .x_row_1(bitwise_or_8_8_2_z_row_1),
    .x_row_2(bitwise_or_8_8_2_z_row_2), .x_row_3(bitwise_or_8_8_2_z_row_3),
    .x_row_4(bitwise_or_8_8_2_z_row_4), .x_row_5(bitwise_or_8_8_2_z_row_5),
    .x_row_6(bitwise_or_8_8_2_z_row_6), .x_row_7(bitwise_or_8_8_2_z_row_7), .y_row_0(x4_row_0),
    .y_row_1(x4_row_1), .y_row_2(x4_row_2), .y_row_3(x4_row_3), .y_row_4(x4_row_4), .y_row_5(x4_row_5),
    .y_row_6(x4_row_6), .y_row_7(x4_row_7), .z_row_0(bitwise_or_8_8_3_z_row_0),
    .z_row_1(bitwise_or_8_8_3_z_row_1), .z_row_2(bitwise_or_8_8_3_z_row_2),
    .z_row_3(bitwise_or_8_8_3_z_row_3), .z_row_4(bitwise_or_8_8_3_z_row_4),
    .z_row_5(bitwise_or_8_8_3_z_row_5), .z_row_6(bitwise_or_8_8_3_z_row_6), .z_row_7(bitwise_or_8_8_3_z_row_7));
  bitwise_or_8_8 bitwise_or_8_8_4 (
    .x_row_0(bitwise_or_8_8_3_z_row_0), .x_row_1(bitwise_or_8_8_3_z_row_1),
    .x_row_2(bitwise_or_8_8_3_z_row_2), .x_row_3(bitwise_or_8_8_3_z_row_3),
    .x_row_4(bitwise_or_8_8_3_z_row_4), .x_row_5(bitwise_or_8_8_3_z_row_5),
    .x_row_6(bitwise_or_8_8_3_z_row_6), .x_row_7(bitwise_or_8_8_3_z_row_7), .y_row_0(x5_row_0),
    .y_row_1(x5_row_1), .y_row_2(x5_row_2), .y_row_3(x5_row_3), .y_row_4(x5_row_4), .y_row_5(x5_row_5),
    .y_row_6(x5_row_6), .y_row_7(x5_row_7), .z_row_0(bitwise_or_8_8_4_z_row_0),
    .z_row_1(bitwise_or_8_8_4_z_row_1), .z_row_2(bitwise_or_8_8_4_z_row_2),
    .z_row_3(bitwise_or_8_8_4_z_row_3), .z_row_4(bitwise_or_8_8_4_z_row_4),
    .z_row_5(bitwise_or_8_8_4_z_row_5), .z_row_6(bitwise_or_8_8_4_z_row_6), .z_row_7(bitwise_or_8_8_4_z_row_7));
  bitwise_or_8_8 bitwise_or_8_8_5 (
    .x_row_0(bitwise_or_8_8_4_z_row_0), .x_row_1(bitwise_or_8_8_4_z_row_1),
    .x_row_2(bitwise_or_8_8_4_z_row_2), .x_row_3(bitwise_or_8_8_4_z_row_3),
    .x_row_4(bitwise_or_8_8_4_z_row_4), .x_row_5(bitwise_or_8_8_4_z_row_5),
    .x_row_6(bitwise_or_8_8_4_z_row_6), .x_row_7(bitwise_or_8_8_4_z_row_7), .y_row_0(x6_row_0),
    .y_row_1(x6_row_1), .y_row_2(x6_row_2), .y_row_3(x6_row_3), .y_row_4(x6_row_4), .y_row_5(x6_row_5),
    .y_row_6(x6_row_6), .y_row_7(x6_row_7), .z_row_0(bitwise_or_8_8_5_z_row_0),
    .z_row_1(bitwise_or_8_8_5_z_row_1), .z_row_2(bitwise_or_8_8_5_z_row_2),
    .z_row_3(bitwise_or_8_8_5_z_row_3), .z_row_4(bitwise_or_8_8_5_z_row_4),
    .z_row_5(bitwise_or_8_8_5_z_row_5), .z_row_6(bitwise_or_8_8_5_z_row_6), .z_row_7(bitwise_or_8_8_5_z_row_7));
  bitwise_or_8_8 bitwise_or_8_8_6 (
    .x_row_0(bitwise_or_8_8_5_z_row_0), .x_row_1(bitwise_or_8_8_5_z_row_1),
    .x_row_2(bitwise_or_8_8_5_z_row_2), .x_row_3(bitwise_or_8_8_5_z_row_3),
    .x_row_4(bitwise_or_8_8_5_z_row_4), .x_row_5(bitwise_or_8_8_5_z_row_5),
    .x_row_6(bitwise_or_8_8_5_z_row_6), .x_row_7(bitwise_or_8_8_5_z_row_7), .y_row_0(x7_row_0),
    .y_row_1(x7_row_1), .y_row_2(x7_row_2), .y_row_3(x7_row_3), .y_row_4(x7_row_4), .y_row_5(x7_row_5),
    .y_row_6(x7_row_6), .y_row_7(x7_row_7), .z_row_0(bitwise_or_8_8_6_z_row_0),
    .z_row_1(bitwise_or_8_8_6_z_row_1), .z_row_2(bitwise_or_8_8_6_z_row_2),
    .z_row_3(bitwise_or_8_8_6_z_row_3), .z_row_4(bitwise_or_8_8_6_z_row_4),
    .z_row_5(bitwise_or_8_8_6_z_row_5), .z_row_6(bitwise_or_8_8_6_z_row_6), .z_row_7(bitwise_or_8_8_6_z_row_7));
  bitwise_or_8_8 bitwise_or_8_8_7 (
    .x_row_0(bitwise_or_8_8_6_z_row_0), .x_row_1(bitwise_or_8_8_6_z_row_1),
    .x_row_2(bitwise_or_8_8_6_z_row_2), .x_row_3(bitwise_or_8_8_6_z_row_3),
    .x_row_4(bitwise_or_8_8_6_z_row_4), .x_row_5(bitwise_or_8_8_6_z_row_5),
    .x_row_6(bitwise_or_8_8_6_z_row_6), .x_row_7(bitwise_or_8_8_6_z_row_7), .y_row_0(8'h80), .y_row_1(8'h40),
    .y_row_2(8'h20), .y_row_3(8'h10), .y_row_4(8'h8), .y_row_5(8'h4), .y_row_6(8'h2), .y_row_7(8'h1),
    .z_row_0(bitwise_or_8_8_7_z_row_0), .z_row_1(bitwise_or_8_8_7_z_row_1),
    .z_row_2(bitwise_or_8_8_7_z_row_2), .z_row_3(bitwise_or_8_8_7_z_row_3),
    .z_row_4(bitwise_or_8_8_7_z_row_4), .z_row_5(bitwise_or_8_8_7_z_row_5),
    .z_row_6(bitwise_or_8_8_7_z_row_6), .z_row_7(bitwise_or_8_8_7_z_row_7));
  matrix_and_8_8 matrix_and_8_8_1 (
    .x_row_0(bitwise_or_8_8_7_z_row_0), .x_row_1(bitwise_or_8_8_7_z_row_1),
    .x_row_2(bitwise_or_8_8_7_z_row_2), .x_row_3(bitwise_or_8_8_7_z_row_3),
    .x_row_4(bitwise_or_8_8_7_z_row_4), .x_row_5(bitwise_or_8_8_7_z_row_5),
    .x_row_6(bitwise_or_8_8_7_z_row_6), .x_row_7(bitwise_or_8_8_7_z_row_7), .z(is_connected));

  // Notes on the sheet:
  //   L = 2
  //   L = 3
  //   L = 4
  //   L = 5
  //   L = 6
  //   L = 7
endmodule

// AND
module matrix_and_8_8 (
  input  [7:0] x_row_0,
  input  [7:0] x_row_1,
  input  [7:0] x_row_2,
  input  [7:0] x_row_3,
  input  [7:0] x_row_4,
  input  [7:0] x_row_5,
  input  [7:0] x_row_6,
  input  [7:0] x_row_7,
  output z
);

  wire [1:0] and_9_out;
  wire [3:0] and_8_out;
  wire [7:0] and_1_out, and_2_out, and_3_out, and_4_out, and_5_out, and_6_out, and_7_out;

  assign and_1_out = x_row_0 & x_row_1;  // AND_Gate and_1, 8 bits wide
  assign and_2_out = x_row_2 & x_row_3;  // AND_Gate and_2, 8 bits wide
  assign and_3_out = x_row_4 & x_row_5;  // AND_Gate and_3, 8 bits wide
  assign and_4_out = x_row_6 & x_row_7;  // AND_Gate and_4, 8 bits wide
  assign and_5_out = and_1_out & and_2_out;  // AND_Gate and_5, 8 bits wide
  assign and_6_out = and_3_out & and_4_out;  // AND_Gate and_6, 8 bits wide
  assign and_7_out = and_5_out & and_6_out;  // AND_Gate and_7, 8 bits wide
  assign and_8_out = and_7_out[3:0] & and_7_out[7:4];  // AND_Gate and_8, 4 bits wide
  DotMatrix #(.inputtype("row"), .matrixcols(8), .matrixrows(8)) dotmatrix_1 (
    .row0(x_row_0), .row1(x_row_1), .row2(x_row_2), .row3(x_row_3), .row4(x_row_4), .row5(x_row_5),
    .row6(x_row_6), .row7(x_row_7));
  assign and_9_out = and_8_out[1:0] & and_8_out[3:2];  // AND_Gate and_9, 2 bits wide
  and and_10 (z, and_9_out[0], and_9_out[1]);
endmodule

module is_fully_connected (
  input  [7:0] x_row_0,
  input  [7:0] x_row_1,
  input  [7:0] x_row_2,
  input  [7:0] x_row_3,
  input  [7:0] x_row_4,
  input  [7:0] x_row_5,
  input  [7:0] x_row_6,
  input  [7:0] x_row_7,
  output is_fully_connected
);

  wire [7:0] bitwise_or_8_8_1_z_row_0, bitwise_or_8_8_1_z_row_1, bitwise_or_8_8_1_z_row_2,
       bitwise_or_8_8_1_z_row_3, bitwise_or_8_8_1_z_row_4, bitwise_or_8_8_1_z_row_5,
       bitwise_or_8_8_1_z_row_6, bitwise_or_8_8_1_z_row_7;

  DotMatrix #(.inputtype("row"), .matrixcols(8), .matrixrows(8)) dotmatrix_1 (
    .row0(x_row_0), .row1(x_row_1), .row2(x_row_2), .row3(x_row_3), .row4(x_row_4), .row5(x_row_5),
    .row6(x_row_6), .row7(x_row_7));
  bitwise_or_8_8 bitwise_or_8_8_1 (
    .x_row_0(8'h80), .x_row_1(8'h40), .x_row_2(8'h20), .x_row_3(8'h10), .x_row_4(8'h8), .x_row_5(8'h4),
    .x_row_6(8'h2), .x_row_7(8'h1), .y_row_0(x_row_0), .y_row_1(x_row_1), .y_row_2(x_row_2),
    .y_row_3(x_row_3), .y_row_4(x_row_4), .y_row_5(x_row_5), .y_row_6(x_row_6), .y_row_7(x_row_7),
    .z_row_0(bitwise_or_8_8_1_z_row_0), .z_row_1(bitwise_or_8_8_1_z_row_1),
    .z_row_2(bitwise_or_8_8_1_z_row_2), .z_row_3(bitwise_or_8_8_1_z_row_3),
    .z_row_4(bitwise_or_8_8_1_z_row_4), .z_row_5(bitwise_or_8_8_1_z_row_5),
    .z_row_6(bitwise_or_8_8_1_z_row_6), .z_row_7(bitwise_or_8_8_1_z_row_7));
  matrix_and_8_8 matrix_and_8_8_1 (
    .x_row_0(bitwise_or_8_8_1_z_row_0), .x_row_1(bitwise_or_8_8_1_z_row_1),
    .x_row_2(bitwise_or_8_8_1_z_row_2), .x_row_3(bitwise_or_8_8_1_z_row_3),
    .x_row_4(bitwise_or_8_8_1_z_row_4), .x_row_5(bitwise_or_8_8_1_z_row_5),
    .x_row_6(bitwise_or_8_8_1_z_row_6), .x_row_7(bitwise_or_8_8_1_z_row_7), .z(is_fully_connected));
endmodule

module exactly (
  input  [7:0] x_row_0,
  input  [7:0] x_row_1,
  input  [7:0] x_row_2,
  input  [7:0] x_row_3,
  input  [7:0] x_row_4,
  input  [7:0] x_row_5,
  input  [7:0] x_row_6,
  input  [7:0] x_row_7,
  input  [2:0] from,
  input  [2:0] to,
  input  [2:0] num_steps,
  output path_exists
);

  wire and_1_out, i_j, x2__i__j, x3__i__j, x4__i__j, x5__i__j, x6__i__j, x7__i__j, x__i__j;
  wire [2:0] xnor_1_out;
  wire [7:0] multiplexer_1_out, multiplexer_3_out, multiplexer_4_out, multiplexer_5_out, multiplexer_11_out,
       multiplexer_13_out, multiplexer_15_out, x2_row_0, x2_row_1, x2_row_2, x2_row_3, x2_row_4, x2_row_5,
       x2_row_6, x2_row_7, x3_row_0, x3_row_1, x3_row_2, x3_row_3, x3_row_4, x3_row_5, x3_row_6, x3_row_7,
       x4_row_0, x4_row_1, x4_row_2, x4_row_3, x4_row_4, x4_row_5, x4_row_6, x4_row_7, x5_row_0, x5_row_1,
       x5_row_2, x5_row_3, x5_row_4, x5_row_5, x5_row_6, x5_row_7, x6_row_0, x6_row_1, x6_row_2, x6_row_3,
       x6_row_4, x6_row_5, x6_row_6, x6_row_7, x7_row_0, x7_row_1, x7_row_2, x7_row_3, x7_row_4, x7_row_5,
       x7_row_6, x7_row_7;

  DotMatrix #(.inputtype("row"), .matrixcols(8), .matrixrows(8)) dotmatrix_1 (
    .row0(x_row_0), .row1(x_row_1), .row2(x_row_2), .row3(x_row_3), .row4(x_row_4), .row5(x_row_5),
    .row6(x_row_6), .row7(x_row_7));
  Multiplexer #(.select(3), .width(8), .enable("false")) multiplexer_1 (
    .in0(x_row_0), .in1(x_row_1), .in2(x_row_2), .in3(x_row_3), .in4(x_row_4), .in5(x_row_5), .in6(x_row_6),
    .in7(x_row_7), .out(multiplexer_1_out), .sel(from));
  matmul matmul_1 (
    .x_row_0(x_row_0), .x_row_1(x_row_1), .x_row_2(x_row_2), .x_row_3(x_row_3), .x_row_4(x_row_4),
    .x_row_5(x_row_5), .x_row_6(x_row_6), .x_row_7(x_row_7), .y_row_0(x_row_0), .y_row_1(x_row_1),
    .y_row_2(x_row_2), .y_row_3(x_row_3), .y_row_4(x_row_4), .y_row_5(x_row_5), .y_row_6(x_row_6),
    .y_row_7(x_row_7), .z_row_0(x2_row_0), .z_row_1(x2_row_1), .z_row_2(x2_row_2), .z_row_3(x2_row_3),
    .z_row_4(x2_row_4), .z_row_5(x2_row_5), .z_row_6(x2_row_6), .z_row_7(x2_row_7));
  matmul matmul_2 (
    .x_row_0(x2_row_0), .x_row_1(x2_row_1), .x_row_2(x2_row_2), .x_row_3(x2_row_3), .x_row_4(x2_row_4),
    .x_row_5(x2_row_5), .x_row_6(x2_row_6), .x_row_7(x2_row_7), .y_row_0(x_row_0), .y_row_1(x_row_1),
    .y_row_2(x_row_2), .y_row_3(x_row_3), .y_row_4(x_row_4), .y_row_5(x_row_5), .y_row_6(x_row_6),
    .y_row_7(x_row_7), .z_row_0(x3_row_0), .z_row_1(x3_row_1), .z_row_2(x3_row_2), .z_row_3(x3_row_3),
    .z_row_4(x3_row_4), .z_row_5(x3_row_5), .z_row_6(x3_row_6), .z_row_7(x3_row_7));
  matmul matmul_3 (
    .x_row_0(x3_row_0), .x_row_1(x3_row_1), .x_row_2(x3_row_2), .x_row_3(x3_row_3), .x_row_4(x3_row_4),
    .x_row_5(x3_row_5), .x_row_6(x3_row_6), .x_row_7(x3_row_7), .y_row_0(x_row_0), .y_row_1(x_row_1),
    .y_row_2(x_row_2), .y_row_3(x_row_3), .y_row_4(x_row_4), .y_row_5(x_row_5), .y_row_6(x_row_6),
    .y_row_7(x_row_7), .z_row_0(x4_row_0), .z_row_1(x4_row_1), .z_row_2(x4_row_2), .z_row_3(x4_row_3),
    .z_row_4(x4_row_4), .z_row_5(x4_row_5), .z_row_6(x4_row_6), .z_row_7(x4_row_7));
  Multiplexer #(.select(3), .enable("false")) multiplexer_2 (
    .in0(multiplexer_1_out[7]), .in1(multiplexer_1_out[6]), .in2(multiplexer_1_out[5]),
    .in3(multiplexer_1_out[4]), .in4(multiplexer_1_out[3]), .in5(multiplexer_1_out[2]),
    .in6(multiplexer_1_out[1]), .in7(multiplexer_1_out[0]), .out(x__i__j), .sel(to));
  assign xnor_1_out = ~(from ^ to);  // XNOR_Gate xnor_1, 3 bits wide
  Multiplexer #(.select(3), .width(8), .enable("false")) multiplexer_3 (
    .in0(x2_row_0), .in1(x2_row_1), .in2(x2_row_2), .in3(x2_row_3), .in4(x2_row_4), .in5(x2_row_5),
    .in6(x2_row_6), .in7(x2_row_7), .out(multiplexer_3_out), .sel(from));
  Multiplexer #(.select(3), .width(8), .enable("false")) multiplexer_4 (
    .in0(x3_row_0), .in1(x3_row_1), .in2(x3_row_2), .in3(x3_row_3), .in4(x3_row_4), .in5(x3_row_5),
    .in6(x3_row_6), .in7(x3_row_7), .out(multiplexer_4_out), .sel(from));
  Multiplexer #(.select(3), .width(8), .enable("false")) multiplexer_5 (
    .in0(x4_row_0), .in1(x4_row_1), .in2(x4_row_2), .in3(x4_row_3), .in4(x4_row_4), .in5(x4_row_5),
    .in6(x4_row_6), .in7(x4_row_7), .out(multiplexer_5_out), .sel(from));
  and and_1 (and_1_out, xnor_1_out[0], xnor_1_out[1]);
  and and_2 (i_j, and_1_out, xnor_1_out[2]);
  Multiplexer #(.select(3), .enable("false")) multiplexer_6 (
    .in0(multiplexer_3_out[7]), .in1(multiplexer_3_out[6]), .in2(multiplexer_3_out[5]),
    .in3(multiplexer_3_out[4]), .in4(multiplexer_3_out[3]), .in5(multiplexer_3_out[2]),
    .in6(multiplexer_3_out[1]), .in7(multiplexer_3_out[0]), .out(x2__i__j), .sel(to));
  Multiplexer #(.select(3), .enable("false")) multiplexer_7 (
    .in0(multiplexer_4_out[7]), .in1(multiplexer_4_out[6]), .in2(multiplexer_4_out[5]),
    .in3(multiplexer_4_out[4]), .in4(multiplexer_4_out[3]), .in5(multiplexer_4_out[2]),
    .in6(multiplexer_4_out[1]), .in7(multiplexer_4_out[0]), .out(x3__i__j), .sel(to));
  Multiplexer #(.select(3), .enable("false")) multiplexer_8 (
    .in0(multiplexer_5_out[7]), .in1(multiplexer_5_out[6]), .in2(multiplexer_5_out[5]),
    .in3(multiplexer_5_out[4]), .in4(multiplexer_5_out[3]), .in5(multiplexer_5_out[2]),
    .in6(multiplexer_5_out[1]), .in7(multiplexer_5_out[0]), .out(x4__i__j), .sel(to));
  matmul matmul_4 (
    .x_row_0(x4_row_0), .x_row_1(x4_row_1), .x_row_2(x4_row_2), .x_row_3(x4_row_3), .x_row_4(x4_row_4),
    .x_row_5(x4_row_5), .x_row_6(x4_row_6), .x_row_7(x4_row_7), .y_row_0(x_row_0), .y_row_1(x_row_1),
    .y_row_2(x_row_2), .y_row_3(x_row_3), .y_row_4(x_row_4), .y_row_5(x_row_5), .y_row_6(x_row_6),
    .y_row_7(x_row_7), .z_row_0(x5_row_0), .z_row_1(x5_row_1), .z_row_2(x5_row_2), .z_row_3(x5_row_3),
    .z_row_4(x5_row_4), .z_row_5(x5_row_5), .z_row_6(x5_row_6), .z_row_7(x5_row_7));
  matmul matmul_5 (
    .x_row_0(x5_row_0), .x_row_1(x5_row_1), .x_row_2(x5_row_2), .x_row_3(x5_row_3), .x_row_4(x5_row_4),
    .x_row_5(x5_row_5), .x_row_6(x5_row_6), .x_row_7(x5_row_7), .y_row_0(x_row_0), .y_row_1(x_row_1),
    .y_row_2(x_row_2), .y_row_3(x_row_3), .y_row_4(x_row_4), .y_row_5(x_row_5), .y_row_6(x_row_6),
    .y_row_7(x_row_7), .z_row_0(x6_row_0), .z_row_1(x6_row_1), .z_row_2(x6_row_2), .z_row_3(x6_row_3),
    .z_row_4(x6_row_4), .z_row_5(x6_row_5), .z_row_6(x6_row_6), .z_row_7(x6_row_7));
  matmul matmul_6 (
    .x_row_0(x6_row_0), .x_row_1(x6_row_1), .x_row_2(x6_row_2), .x_row_3(x6_row_3), .x_row_4(x6_row_4),
    .x_row_5(x6_row_5), .x_row_6(x6_row_6), .x_row_7(x6_row_7), .y_row_0(x_row_0), .y_row_1(x_row_1),
    .y_row_2(x_row_2), .y_row_3(x_row_3), .y_row_4(x_row_4), .y_row_5(x_row_5), .y_row_6(x_row_6),
    .y_row_7(x_row_7), .z_row_0(x7_row_0), .z_row_1(x7_row_1), .z_row_2(x7_row_2), .z_row_3(x7_row_3),
    .z_row_4(x7_row_4), .z_row_5(x7_row_5), .z_row_6(x7_row_6), .z_row_7(x7_row_7));
  Multiplexer #(.select(3), .enable("false")) multiplexer_9 (
    .in0(i_j), .in1(x__i__j), .in2(x2__i__j), .in3(x3__i__j), .in4(x4__i__j), .in5(x5__i__j), .in6(x6__i__j),
    .in7(x7__i__j), .out(path_exists), .sel(num_steps));
  Multiplexer #(.select(3), .enable("false")) multiplexer_10 (
    .in0(multiplexer_11_out[7]), .in1(multiplexer_11_out[6]), .in2(multiplexer_11_out[5]),
    .in3(multiplexer_11_out[4]), .in4(multiplexer_11_out[3]), .in5(multiplexer_11_out[2]),
    .in6(multiplexer_11_out[1]), .in7(multiplexer_11_out[0]), .out(x5__i__j), .sel(to));
  Multiplexer #(.select(3), .width(8), .enable("false")) multiplexer_11 (
    .in0(x5_row_0), .in1(x5_row_1), .in2(x5_row_2), .in3(x5_row_3), .in4(x5_row_4), .in5(x5_row_5),
    .in6(x5_row_6), .in7(x5_row_7), .out(multiplexer_11_out), .sel(from));
  Multiplexer #(.select(3), .enable("false")) multiplexer_12 (
    .in0(multiplexer_13_out[7]), .in1(multiplexer_13_out[6]), .in2(multiplexer_13_out[5]),
    .in3(multiplexer_13_out[4]), .in4(multiplexer_13_out[3]), .in5(multiplexer_13_out[2]),
    .in6(multiplexer_13_out[1]), .in7(multiplexer_13_out[0]), .out(x6__i__j), .sel(to));
  Multiplexer #(.select(3), .width(8), .enable("false")) multiplexer_13 (
    .in0(x6_row_0), .in1(x6_row_1), .in2(x6_row_2), .in3(x6_row_3), .in4(x6_row_4), .in5(x6_row_5),
    .in6(x6_row_6), .in7(x6_row_7), .out(multiplexer_13_out), .sel(from));
  Multiplexer #(.select(3), .enable("false")) multiplexer_14 (
    .in0(multiplexer_15_out[7]), .in1(multiplexer_15_out[6]), .in2(multiplexer_15_out[5]),
    .in3(multiplexer_15_out[4]), .in4(multiplexer_15_out[3]), .in5(multiplexer_15_out[2]),
    .in6(multiplexer_15_out[1]), .in7(multiplexer_15_out[0]), .out(x7__i__j), .sel(to));
  Multiplexer #(.select(3), .width(8), .enable("false")) multiplexer_15 (
    .in0(x7_row_0), .in1(x7_row_1), .in2(x7_row_2), .in3(x7_row_3), .in4(x7_row_4), .in5(x7_row_5),
    .in6(x7_row_6), .in7(x7_row_7), .out(multiplexer_15_out), .sel(from));

  // Notes on the sheet:
  //   L = 1
  //   L = 2
  //   L = 3
  //   L = 4
  //   L = 0
  //   bit choosing
  //   L = 5
  //   L = 6
  //   L = 7
endmodule

module atmost (
  input  [7:0] x_row_0,
  input  [7:0] x_row_1,
  input  [7:0] x_row_2,
  input  [7:0] x_row_3,
  input  [7:0] x_row_4,
  input  [7:0] x_row_5,
  input  [7:0] x_row_6,
  input  [7:0] x_row_7,
  input  [2:0] from,
  input  [2:0] to,
  input  [2:0] num_steps,
  output path_exists
);

  wire and_1_out, i_j, or_1_out, or_2_out, or_3_out, or_4_out, or_5_out, or_6_out, or_7_out, x2__i__j,
       x3__i__j, x4__i__j, x5__i__j, x6__i__j, x7__i__j, x__i__j;
  wire [2:0] xnor_1_out;
  wire [7:0] multiplexer_2_out, multiplexer_3_out, multiplexer_4_out, multiplexer_5_out, multiplexer_9_out,
       multiplexer_10_out, multiplexer_11_out, x2_row_0, x2_row_1, x2_row_2, x2_row_3, x2_row_4, x2_row_5,
       x2_row_6, x2_row_7, x3_row_0, x3_row_1, x3_row_2, x3_row_3, x3_row_4, x3_row_5, x3_row_6, x3_row_7,
       x4_row_0, x4_row_1, x4_row_2, x4_row_3, x4_row_4, x4_row_5, x4_row_6, x4_row_7, x5_row_0, x5_row_1,
       x5_row_2, x5_row_3, x5_row_4, x5_row_5, x5_row_6, x5_row_7, x6_row_0, x6_row_1, x6_row_2, x6_row_3,
       x6_row_4, x6_row_5, x6_row_6, x6_row_7, x7_row_0, x7_row_1, x7_row_2, x7_row_3, x7_row_4, x7_row_5,
       x7_row_6, x7_row_7;

  assign xnor_1_out = ~(from ^ to);  // XNOR_Gate xnor_1, 3 bits wide
  DotMatrix #(.inputtype("row"), .matrixcols(8), .matrixrows(8)) dotmatrix_1 (
    .row0(x_row_0), .row1(x_row_1), .row2(x_row_2), .row3(x_row_3), .row4(x_row_4), .row5(x_row_5),
    .row6(x_row_6), .row7(x_row_7));
  and and_1 (and_1_out, xnor_1_out[0], xnor_1_out[1]);
  Multiplexer #(.select(3), .enable("false")) multiplexer_1 (
    .in0(multiplexer_2_out[7]), .in1(multiplexer_2_out[6]), .in2(multiplexer_2_out[5]),
    .in3(multiplexer_2_out[4]), .in4(multiplexer_2_out[3]), .in5(multiplexer_2_out[2]),
    .in6(multiplexer_2_out[1]), .in7(multiplexer_2_out[0]), .out(x__i__j), .sel(to));
  Multiplexer #(.select(3), .width(8), .enable("false")) multiplexer_2 (
    .in0(x_row_0), .in1(x_row_1), .in2(x_row_2), .in3(x_row_3), .in4(x_row_4), .in5(x_row_5), .in6(x_row_6),
    .in7(x_row_7), .out(multiplexer_2_out), .sel(from));
  matmul matmul_1 (
    .x_row_0(x_row_0), .x_row_1(x_row_1), .x_row_2(x_row_2), .x_row_3(x_row_3), .x_row_4(x_row_4),
    .x_row_5(x_row_5), .x_row_6(x_row_6), .x_row_7(x_row_7), .y_row_0(x_row_0), .y_row_1(x_row_1),
    .y_row_2(x_row_2), .y_row_3(x_row_3), .y_row_4(x_row_4), .y_row_5(x_row_5), .y_row_6(x_row_6),
    .y_row_7(x_row_7), .z_row_0(x2_row_0), .z_row_1(x2_row_1), .z_row_2(x2_row_2), .z_row_3(x2_row_3),
    .z_row_4(x2_row_4), .z_row_5(x2_row_5), .z_row_6(x2_row_6), .z_row_7(x2_row_7));
  matmul matmul_2 (
    .x_row_0(x2_row_0), .x_row_1(x2_row_1), .x_row_2(x2_row_2), .x_row_3(x2_row_3), .x_row_4(x2_row_4),
    .x_row_5(x2_row_5), .x_row_6(x2_row_6), .x_row_7(x2_row_7), .y_row_0(x_row_0), .y_row_1(x_row_1),
    .y_row_2(x_row_2), .y_row_3(x_row_3), .y_row_4(x_row_4), .y_row_5(x_row_5), .y_row_6(x_row_6),
    .y_row_7(x_row_7), .z_row_0(x3_row_0), .z_row_1(x3_row_1), .z_row_2(x3_row_2), .z_row_3(x3_row_3),
    .z_row_4(x3_row_4), .z_row_5(x3_row_5), .z_row_6(x3_row_6), .z_row_7(x3_row_7));
  matmul matmul_3 (
    .x_row_0(x3_row_0), .x_row_1(x3_row_1), .x_row_2(x3_row_2), .x_row_3(x3_row_3), .x_row_4(x3_row_4),
    .x_row_5(x3_row_5), .x_row_6(x3_row_6), .x_row_7(x3_row_7), .y_row_0(x_row_0), .y_row_1(x_row_1),
    .y_row_2(x_row_2), .y_row_3(x_row_3), .y_row_4(x_row_4), .y_row_5(x_row_5), .y_row_6(x_row_6),
    .y_row_7(x_row_7), .z_row_0(x4_row_0), .z_row_1(x4_row_1), .z_row_2(x4_row_2), .z_row_3(x4_row_3),
    .z_row_4(x4_row_4), .z_row_5(x4_row_5), .z_row_6(x4_row_6), .z_row_7(x4_row_7));
  and and_2 (i_j, and_1_out, xnor_1_out[2]);
  Multiplexer #(.select(3), .width(8), .enable("false")) multiplexer_3 (
    .in0(x2_row_0), .in1(x2_row_1), .in2(x2_row_2), .in3(x2_row_3), .in4(x2_row_4), .in5(x2_row_5),
    .in6(x2_row_6), .in7(x2_row_7), .out(multiplexer_3_out), .sel(from));
  Multiplexer #(.select(3), .width(8), .enable("false")) multiplexer_4 (
    .in0(x3_row_0), .in1(x3_row_1), .in2(x3_row_2), .in3(x3_row_3), .in4(x3_row_4), .in5(x3_row_5),
    .in6(x3_row_6), .in7(x3_row_7), .out(multiplexer_4_out), .sel(from));
  Multiplexer #(.select(3), .width(8), .enable("false")) multiplexer_5 (
    .in0(x4_row_0), .in1(x4_row_1), .in2(x4_row_2), .in3(x4_row_3), .in4(x4_row_4), .in5(x4_row_5),
    .in6(x4_row_6), .in7(x4_row_7), .out(multiplexer_5_out), .sel(from));
  Multiplexer #(.select(3), .enable("false")) multiplexer_6 (
    .in0(multiplexer_3_out[7]), .in1(multiplexer_3_out[6]), .in2(multiplexer_3_out[5]),
    .in3(multiplexer_3_out[4]), .in4(multiplexer_3_out[3]), .in5(multiplexer_3_out[2]),
    .in6(multiplexer_3_out[1]), .in7(multiplexer_3_out[0]), .out(x2__i__j), .sel(to));
  Multiplexer #(.select(3), .enable("false")) multiplexer_7 (
    .in0(multiplexer_4_out[7]), .in1(multiplexer_4_out[6]), .in2(multiplexer_4_out[5]),
    .in3(multiplexer_4_out[4]), .in4(multiplexer_4_out[3]), .in5(multiplexer_4_out[2]),
    .in6(multiplexer_4_out[1]), .in7(multiplexer_4_out[0]), .out(x3__i__j), .sel(to));
  Multiplexer #(.select(3), .enable("false")) multiplexer_8 (
    .in0(multiplexer_5_out[7]), .in1(multiplexer_5_out[6]), .in2(multiplexer_5_out[5]),
    .in3(multiplexer_5_out[4]), .in4(multiplexer_5_out[3]), .in5(multiplexer_5_out[2]),
    .in6(multiplexer_5_out[1]), .in7(multiplexer_5_out[0]), .out(x4__i__j), .sel(to));
  or or_1 (or_1_out, i_j, x__i__j);
  or or_2 (or_2_out, or_1_out, x2__i__j);
  matmul matmul_4 (
    .x_row_0(x4_row_0), .x_row_1(x4_row_1), .x_row_2(x4_row_2), .x_row_3(x4_row_3), .x_row_4(x4_row_4),
    .x_row_5(x4_row_5), .x_row_6(x4_row_6), .x_row_7(x4_row_7), .y_row_0(x_row_0), .y_row_1(x_row_1),
    .y_row_2(x_row_2), .y_row_3(x_row_3), .y_row_4(x_row_4), .y_row_5(x_row_5), .y_row_6(x_row_6),
    .y_row_7(x_row_7), .z_row_0(x5_row_0), .z_row_1(x5_row_1), .z_row_2(x5_row_2), .z_row_3(x5_row_3),
    .z_row_4(x5_row_4), .z_row_5(x5_row_5), .z_row_6(x5_row_6), .z_row_7(x5_row_7));
  matmul matmul_5 (
    .x_row_0(x5_row_0), .x_row_1(x5_row_1), .x_row_2(x5_row_2), .x_row_3(x5_row_3), .x_row_4(x5_row_4),
    .x_row_5(x5_row_5), .x_row_6(x5_row_6), .x_row_7(x5_row_7), .y_row_0(x_row_0), .y_row_1(x_row_1),
    .y_row_2(x_row_2), .y_row_3(x_row_3), .y_row_4(x_row_4), .y_row_5(x_row_5), .y_row_6(x_row_6),
    .y_row_7(x_row_7), .z_row_0(x6_row_0), .z_row_1(x6_row_1), .z_row_2(x6_row_2), .z_row_3(x6_row_3),
    .z_row_4(x6_row_4), .z_row_5(x6_row_5), .z_row_6(x6_row_6), .z_row_7(x6_row_7));
  matmul matmul_6 (
    .x_row_0(x6_row_0), .x_row_1(x6_row_1), .x_row_2(x6_row_2), .x_row_3(x6_row_3), .x_row_4(x6_row_4),
    .x_row_5(x6_row_5), .x_row_6(x6_row_6), .x_row_7(x6_row_7), .y_row_0(x_row_0), .y_row_1(x_row_1),
    .y_row_2(x_row_2), .y_row_3(x_row_3), .y_row_4(x_row_4), .y_row_5(x_row_5), .y_row_6(x_row_6),
    .y_row_7(x_row_7), .z_row_0(x7_row_0), .z_row_1(x7_row_1), .z_row_2(x7_row_2), .z_row_3(x7_row_3),
    .z_row_4(x7_row_4), .z_row_5(x7_row_5), .z_row_6(x7_row_6), .z_row_7(x7_row_7));
  or or_3 (or_3_out, or_2_out, x3__i__j);
  or or_4 (or_4_out, or_3_out, x4__i__j);
  or or_5 (or_5_out, or_4_out, x5__i__j);
  or or_6 (or_6_out, or_5_out, x6__i__j);
  or or_7 (or_7_out, or_6_out, x7__i__j);
  Multiplexer #(.select(3), .width(8), .enable("false")) multiplexer_9 (
    .in0(x5_row_0), .in1(x5_row_1), .in2(x5_row_2), .in3(x5_row_3), .in4(x5_row_4), .in5(x5_row_5),
    .in6(x5_row_6), .in7(x5_row_7), .out(multiplexer_9_out), .sel(from));
  Multiplexer #(.select(3), .width(8), .enable("false")) multiplexer_10 (
    .in0(x6_row_0), .in1(x6_row_1), .in2(x6_row_2), .in3(x6_row_3), .in4(x6_row_4), .in5(x6_row_5),
    .in6(x6_row_6), .in7(x6_row_7), .out(multiplexer_10_out), .sel(from));
  Multiplexer #(.select(3), .width(8), .enable("false")) multiplexer_11 (
    .in0(x7_row_0), .in1(x7_row_1), .in2(x7_row_2), .in3(x7_row_3), .in4(x7_row_4), .in5(x7_row_5),
    .in6(x7_row_6), .in7(x7_row_7), .out(multiplexer_11_out), .sel(from));
  Multiplexer #(.select(3), .enable("false")) multiplexer_12 (
    .in0(multiplexer_9_out[7]), .in1(multiplexer_9_out[6]), .in2(multiplexer_9_out[5]),
    .in3(multiplexer_9_out[4]), .in4(multiplexer_9_out[3]), .in5(multiplexer_9_out[2]),
    .in6(multiplexer_9_out[1]), .in7(multiplexer_9_out[0]), .out(x5__i__j), .sel(to));
  Multiplexer #(.select(3), .enable("false")) multiplexer_13 (
    .in0(multiplexer_10_out[7]), .in1(multiplexer_10_out[6]), .in2(multiplexer_10_out[5]),
    .in3(multiplexer_10_out[4]), .in4(multiplexer_10_out[3]), .in5(multiplexer_10_out[2]),
    .in6(multiplexer_10_out[1]), .in7(multiplexer_10_out[0]), .out(x6__i__j), .sel(to));
  Multiplexer #(.select(3), .enable("false")) multiplexer_14 (
    .in0(multiplexer_11_out[7]), .in1(multiplexer_11_out[6]), .in2(multiplexer_11_out[5]),
    .in3(multiplexer_11_out[4]), .in4(multiplexer_11_out[3]), .in5(multiplexer_11_out[2]),
    .in6(multiplexer_11_out[1]), .in7(multiplexer_11_out[0]), .out(x7__i__j), .sel(to));
  Multiplexer #(.select(3), .enable("false")) multiplexer_15 (
    .in0(i_j), .in1(or_1_out), .in2(or_2_out), .in3(or_3_out), .in4(or_4_out), .in5(or_5_out),
    .in6(or_6_out), .in7(or_7_out), .out(path_exists), .sel(num_steps));

  // Notes on the sheet:
  //   L = 1
  //   L = 2
  //   L = 3
  //   L = 4
  //   L = 5
  //   L = 6
  //   L = 7
endmodule
