// Logisim project 206722894_recursion.circ as structural Verilog: 26 circuits, main circuit matmul
module matmul (
  input  [7:0] x_row_0,
  input  [7:0] x_row_1,
  input  [7:0] x_row_2,
  input  [7:0] x_row_3,
  input  [7:0] x_row_4,
  input  [7:0] x_row_5,
  input  [7:0] x_row_6,
  input  [7:0] x_row_7,
  input  [7:0] y_row_0,
  input  [7:0] y_row_1,
  input  [7:0] y_row_2,
  input  [7:0] y_row_3,
  input  [7:0] y_row_4,
  input  [7:0] y_row_5,
  input  [7:0] y_row_6,
  input  [7:0] y_row_7,
  output [7:0] z_row_0,
  output [7:0] z_row_1,
  output [7:0] z_row_2,
  output [7:0] z_row_3,
  output [7:0] z_row_4,
  output [7:0] z_row_5,
  output [7:0] z_row_6,
  output [7:0] z_row_7
);

  wire [7:0] y_col_0, y_col_1, y_col_2, y_col_3, y_col_4, y_col_5, y_col_6, y_col_7;

  matmul_step_2 matmul_step_2_1 (
    .row(x_row_0), .col_0(y_col_0), .col_1(y_col_1), .col_2(y_col_2), .col_3(y_col_3), .col_4(y_col_4),
    .col_5(y_col_5), .col_6(y_col_6), .col_7(y_col_7), .product_row(z_row_0));
  matmul_step_2 matmul_step_2_2 (
    .row(x_row_1), .col_0(y_col_0), .col_1(y_col_1), .col_2(y_col_2), .col_3(y_col_3), .col_4(y_col_4),
    .col_5(y_col_5), .col_6(y_col_6), .col_7(y_col_7), .product_row(z_row_1));
  matmul_step_2 matmul_step_2_3 (
    .row(x_row_2), .col_0(y_col_0), .col_1(y_col_1), .col_2(y_col_2), .col_3(y_col_3), .col_4(y_col_4),
    .col_5(y_col_5), .col_6(y_col_6), .col_7(y_col_7), .product_row(z_row_2));
  DotMatrix #(.inputtype("row"), .matrixcols(8), .matrixrows(8)) dotmatrix_1 (
    .row0(x_row_0), .row1(x_row_1), .row2(x_row_2), .row3(x_row_3), .row4(x_row_4), .row5(x_row_5),
    .row6(x_row_6), .row7(x_row_7));
  DotMatrix #(.inputtype("row"), .matrixcols(8), .matrixrows(8)) dotmatrix_2 (
    .row0(y_row_0), .row1(y_row_1), .row2(y_row_2), .row3(y_row_3), .row4(y_row_4), .row5(y_row_5),
    .row6(y_row_6), .row7(y_row_7));
  matmul_step_2 matmul_step_2_4 (
    .row(x_row_3), .col_0(y_col_0), .col_1(y_col_1), .col_2(y_col_2), .col_3(y_col_3), .col_4(y_col_4),
    .col_5(y_col_5), .col_6(y_col_6), .col_7(y_col_7), .product_row(z_row_3));
  matmul_step_2 matmul_step_2_5 (
    .row(x_row_4), .col_0(y_col_0), .col_1(y_col_1), .col_2(y_col_2), .col_3(y_col_3), .col_4(y_col_4),
    .col_5(y_col_5), .col_6(y_col_6), .col_7(y_col_7), .product_row(z_row_4));
  matmul_step_2 matmul_step_2_6 (
    .row(x_row_5), .col_0(y_col_0), .col_1(y_col_1), .col_2(y_col_2), .col_3(y_col_3), .col_4(y_col_4),
    .col_5(y_col_5), .col_6(y_col_6), .col_7(y_col_7), .product_row(z_row_5));
  DotMatrix #(.inputtype("row"), .matrixcols(8), .matrixrows(8)) dotmatrix_3 (
    .row0(z_row_0), .row1(z_row_1), .row2(z_row_2), .row3(z_row_3), .row4(z_row_4), .row5(z_row_5),
    .row6(z_row_6), .row7(z_row_7));
  matmul_step_2 matmul_step_2_7 (
    .row(x_row_6), .col_0(y_col_0), .col_1(y_col_1), .col_2(y_col_2), .col_3(y_col_3), .col_4(y_col_4),
    .col_5(y_col_5), .col_6(y_col_6), .col_7(y_col_7), .product_row(z_row_6));
  matmul_step_2 matmul_step_2_8 (
    .row(x_row_7), .col_0(y_col_0), .col_1(y_col_1), .col_2(y_col_2), .col_3(y_col_3), .col_4(y_col_4),
    .col_5(y_col_5), .col_6(y_col_6), .col_7(y_col_7), .product_row(z_row_7));
  transpose transpose_1 (
    .row_0(y_row_0), .row_1(y_row_1), .row_2(y_row_2), .row_3(y_row_3), .row_4(y_row_4), .row_5(y_row_5),
    .row_6(y_row_6), .row_7(y_row_7), .column_0(y_col_0), .column_1(y_col_1), .column_2(y_col_2),
    .column_3(y_col_3), .column_4(y_col_4), .column_5(y_col_5), .column_6(y_col_6), .column_7(y_col_7));
endmodule

module transpose (
  input  [7:0] row_0,
  input  [7:0] row_1,
  input  [7:0] row_2,
  input  [7:0] row_3,
  input  [7:0] row_4,
  input  [7:0] row_5,
  input  [7:0] row_6,
  input  [7:0] row_7,
  output [7:0] column_0,
  output [7:0] column_1,
  output [7:0] column_2,
  output [7:0] column_3,
  output [7:0] column_4,
  output [7:0] column_5,
  output [7:0] column_6,
  output [7:0] column_7
);

  extract_col extract_col_1 (
    .in_1(3'b000), .row_0(row_0), .row_1(row_1), .row_2(row_2), .row_3(row_3), .row_4(row_4), .row_5(row_5),
    .row_6(row_6), .row_7(row_7), .b(column_0));
  extract_col extract_col_2 (
    .in_1(3'b100), .row_0(row_0), .row_1(row_1), .row_2(row_2), .row_3(row_3), .row_4(row_4), .row_5(row_5),
    .row_6(row_6), .row_7(row_7), .b(column_4));
  extract_col extract_col_3 (
    .in_1(3'b001), .row_0(row_0), .row_1(row_1), .row_2(row_2), .row_3(row_3), .row_4(row_4), .row_5(row_5),
    .row_6(row_6), .row_7(row_7), .b(column_1));
  extract_col extract_col_4 (
    .in_1(3'b101), .row_0(row_0), .row_1(row_1), .row_2(row_2), .row_3(row_3), .row_4(row_4), .row_5(row_5),
    .row_6(row_6), .row_7(row_7), .b(column_5));
  extract_col extract_col_5 (
    .in_1(3'b010), .row_0(row_0), .row_1(row_1), .row_2(row_2), .row_3(row_3), .row_4(row_4), .row_5(row_5),
    .row_6(row_6), .row_7(row_7), .b(column_2));
  extract_col extract_col_6 (
    .in_1(3'b110), .row_0(row_0), .row_1(row_1), .row_2(row_2), .row_3(row_3), .row_4(row_4), .row_5(row_5),
    .row_6(row_6), .row_7(row_7), .b(column_6));
  extract_col extract_col_7 (
    .in_1(3'b011), .row_0(row_0), .row_1(row_1), .row_2(row_2), .row_3(row_3), .row_4(row_4), .row_5(row_5),
    .row_6(row_6), .row_7(row_7), .b(column_3));
  extract_col extract_col_8 (
    .in_1(3'b111), .row_0(row_0), .row_1(row_1), .row_2(row_2), .row_3(row_3), .row_4(row_4), .row_5(row_5),
    .row_6(row_6), .row_7(row_7), .b(column_7));
endmodule

module extract_col (
  input  [2:0] in_1,
  input  [7:0] row_0,
  input  [7:0] row_1,
  input  [7:0] row_2,
  input  [7:0] row_3,
  input  [7:0] row_4,
  input  [7:0] row_5,
  input  [7:0] row_6,
  input  [7:0] row_7,
  output [7:0] b
);

  wire [2:0] not_1_out, not_2_out, not_3_out, not_4_out, not_5_out, not_6_out, not_7_out, not_8_out;

  BitSelector bitselector_1 (.in(row_0), .out(b[7]), .sel(not_1_out));
  assign not_1_out = ~in_1;  // NOT_Gate not_1, 3 bits wide
  BitSelector bitselector_2 (.in(row_1), .out(b[6]), .sel(not_2_out));
  assign not_2_out = ~in_1;  // NOT_Gate not_2, 3 bits wide
  BitSelector bitselector_3 (.in(row_2), .out(b[5]), .sel(not_3_out));
  assign not_3_out = ~in_1;  // NOT_Gate not_3, 3 bits wide
  BitSelector bitselector_4 (.in(row_3), .out(b[4]), .sel(not_4_out));
  assign not_4_out = ~in_1;  // NOT_Gate not_4, 3 bits wide
  BitSelector bitselector_5 (.in(row_4), .out(b[3]), .sel(not_5_out));
  assign not_5_out = ~in_1;  // NOT_Gate not_5, 3 bits wide
  BitSelector bitselector_6 (.in(row_5), .out(b[2]), .sel(not_6_out));
  assign not_6_out = ~in_1;  // NOT_Gate not_6, 3 bits wide
  BitSelector bitselector_7 (.in(row_6), .out(b[1]), .sel(not_7_out));
  assign not_7_out = ~in_1;  // NOT_Gate not_7, 3 bits wide
  BitSelector bitselector_8 (.in(row_7), .out(b[0]), .sel(not_8_out));
  assign not_8_out = ~in_1;  // NOT_Gate not_8, 3 bits wide

  // Other names for the same wires on the sheet: col[7:0] = b; col_num[2:0] = in_1
endmodule

module matmul_step_1 (
  input  [7:0] row,
  input  [7:0] col,
  output \output 
);

  wire and_1_out, and_2_out, and_3_out, and_4_out, and_5_out, and_6_out, and_7_out, and_8_out, or_1_out,
       or_2_out, or_3_out, or_4_out, or_5_out, or_6_out;

  and and_1 (and_1_out, row[0], col[0]);
  and and_2 (and_2_out, row[1], col[1]);
  and and_3 (and_3_out, row[2], col[2]);
  and and_4 (and_4_out, row[3], col[3]);
  and and_5 (and_5_out, row[4], col[4]);
  and and_6 (and_6_out, row[5], col[5]);
  and and_7 (and_7_out, row[6], col[6]);
  and and_8 (and_8_out, row[7], col[7]);
  or or_1 (or_1_out, and_1_out, and_2_out);
  or or_2 (or_2_out, and_3_out, and_4_out);
  or or_3 (or_3_out, and_5_out, and_6_out);
  or or_4 (or_4_out, and_7_out, and_8_out);
  or or_5 (or_5_out, or_1_out, or_2_out);
  or or_6 (or_6_out, or_3_out, or_4_out);
  or or_7 (\output , or_5_out, or_6_out);

  // Other names for the same wires on the sheet: col_0 = col[0]; col_1 = col[1]; col_2 = col[2]; col_3 = col[3];
  //   col_4 = col[4]; col_5 = col[5]; col_6 = col[6]; col_7 = col[7]; row_0 = row[0]; row_1 = row[1]; row_2 = row[2];
  //   row_3 = row[3]; row_4 = row[4]; row_5 = row[5]; row_6 = row[6]; row_7 = row[7]
endmodule

module matmul_step_2 (
  input  [7:0] row,
  input  [7:0] col_0,
  input  [7:0] col_1,
  input  [7:0] col_2,
  input  [7:0] col_3,
  input  [7:0] col_4,
  input  [7:0] col_5,
  input  [7:0] col_6,
  input  [7:0] col_7,
  output [7:0] product_row
);

  matmul_step_1 matmul_step_1_1 (.row(row), .col(col_0), .\output (product_row[7]));
  matmul_step_1 matmul_step_1_2 (.row(row), .col(col_1), .\output (product_row[6]));
  matmul_step_1 matmul_step_1_3 (.row(row), .col(col_2), .\output (product_row[5]));
  matmul_step_1 matmul_step_1_4 (.row(row), .col(col_3), .\output (product_row[4]));
  matmul_step_1 matmul_step_1_5 (.row(row), .col(col_4), .\output (product_row[3]));
  matmul_step_1 matmul_step_1_6 (.row(row), .col(col_5), .\output (product_row[2]));
  matmul_step_1 matmul_step_1_7 (.row(row), .col(col_6), .\output (product_row[1]));
  matmul_step_1 matmul_step_1_8 (.row(row), .col(col_7), .\output (product_row[0]));
endmodule

module pow_0 (
  input  [7:0] x_row_0,
  input  [7:0] x_row_1,
  input  [7:0] x_row_2,
  input  [7:0] x_row_3,
  input  [7:0] x_row_4,
  input  [7:0] x_row_5,
  input  [7:0] x_row_6,
  input  [7:0] x_row_7,
  output [7:0] z_row_0,
  output [7:0] z_row_1,
  output [7:0] z_row_2,
  output [7:0] z_row_3,
  output [7:0] z_row_4,
  output [7:0] z_row_5,
  output [7:0] z_row_6,
  output [7:0] z_row_7
);

  DotMatrix #(.inputtype("row"), .matrixcols(8), .matrixrows(8)) dotmatrix_1 (
    .row0(x_row_0), .row1(x_row_1), .row2(x_row_2), .row3(x_row_3), .row4(x_row_4), .row5(x_row_5),
    .row6(x_row_6), .row7(x_row_7));
  DotMatrix #(.inputtype("row"), .matrixcols(8), .matrixrows(8)) dotmatrix_2 (
    .row0(8'h80), .row1(8'h40), .row2(8'h20), .row3(8'h10), .row4(8'h8), .row5(8'h4), .row6(8'h2), .row7(8'h1));

  assign z_row_0 = 8'h80;
  assign z_row_1 = 8'h40;
  assign z_row_2 = 8'h20;
  assign z_row_3 = 8'h10;
  assign z_row_4 = 8'h8;
  assign z_row_5 = 8'h4;
  assign z_row_6 = 8'h2;
  assign z_row_7 = 8'h1;
endmodule

module pow_1 (
  input  [7:0] x_row_0,
  input  [7:0] x_row_1,
  input  [7:0] x_row_2,
  input  [7:0] x_row_3,
  input  [7:0] x_row_4,
  input  [7:0] x_row_5,
  input  [7:0] x_row_6,
  input  [7:0] x_row_7,
  output [7:0] z_row_0,
  output [7:0] z_row_1,
  output [7:0] z_row_2,
  output [7:0] z_row_3,
  output [7:0] z_row_4,
  output [7:0] z_row_5,
  output [7:0] z_row_6,
  output [7:0] z_row_7
);

  DotMatrix #(.inputtype("row"), .matrixcols(8), .matrixrows(8)) dotmatrix_1 (
    .row0(x_row_0), .row1(x_row_1), .row2(x_row_2), .row3(x_row_3), .row4(x_row_4), .row5(x_row_5),
    .row6(x_row_6), .row7(x_row_7));
  DotMatrix #(.inputtype("row"), .matrixcols(8), .matrixrows(8)) dotmatrix_2 (
    .row0(x_row_0), .row1(x_row_1), .row2(x_row_2), .row3(x_row_3), .row4(x_row_4), .row5(x_row_5),
    .row6(x_row_6), .row7(x_row_7));

  assign z_row_0 = x_row_0;
  assign z_row_1 = x_row_1;
  assign z_row_2 = x_row_2;
  assign z_row_3 = x_row_3;
  assign z_row_4 = x_row_4;
  assign z_row_5 = x_row_5;
  assign z_row_6 = x_row_6;
  assign z_row_7 = x_row_7;
endmodule

module pow_2 (
  input  [7:0] x_row_0,
  input  [7:0] x_row_1,
  input  [7:0] x_row_2,
  input  [7:0] x_row_3,
  input  [7:0] x_row_4,
  input  [7:0] x_row_5,
  input  [7:0] x_row_6,
  input  [7:0] x_row_7,
  output [7:0] z_row_0,
  output [7:0] z_row_1,
  output [7:0] z_row_2,
  output [7:0] z_row_3,
  output [7:0] z_row_4,
  output [7:0] z_row_5,
  output [7:0] z_row_6,
  output [7:0] z_row_7
);

  DotMatrix #(.inputtype("row"), .matrixcols(8), .matrixrows(8)) dotmatrix_1 (
    .row0(x_row_0), .row1(x_row_1), .row2(x_row_2), .row3(x_row_3), .row4(x_row_4), .row5(x_row_5),
    .row6(x_row_6), .row7(x_row_7));
  DotMatrix #(.inputtype("row"), .matrixcols(8), .matrixrows(8)) dotmatrix_2 (
    .row0(z_row_0), .row1(z_row_1), .row2(z_row_2), .row3(z_row_3), .row4(z_row_4), .row5(z_row_5),
    .row6(z_row_6), .row7(z_row_7));
  matmul matmul_1 (
    .x_row_0(x_row_0), .x_row_1(x_row_1), .x_row_2(x_row_2), .x_row_3(x_row_3), .x_row_4(x_row_4),
    .x_row_5(x_row_5), .x_row_6(x_row_6), .x_row_7(x_row_7), .y_row_0(x_row_0), .y_row_1(x_row_1),
    .y_row_2(x_row_2), .y_row_3(x_row_3), .y_row_4(x_row_4), .y_row_5(x_row_5), .y_row_6(x_row_6),
    .y_row_7(x_row_7), .z_row_0(z_row_0), .z_row_1(z_row_1), .z_row_2(z_row_2), .z_row_3(z_row_3),
    .z_row_4(z_row_4), .z_row_5(z_row_5), .z_row_6(z_row_6), .z_row_7(z_row_7));

  // Notes on the sheet:
  //   K = 2
endmodule

module pow_3 (
  input  [7:0] x_row_0,
  input  [7:0] x_row_1,
  input  [7:0] x_row_2,
  input  [7:0] x_row_3,
  input  [7:0] x_row_4,
  input  [7:0] x_row_5,
  input  [7:0] x_row_6,
  input  [7:0] x_row_7,
  output [7:0] z_row_0,
  output [7:0] z_row_1,
  output [7:0] z_row_2,
  output [7:0] z_row_3,
  output [7:0] z_row_4,
  output [7:0] z_row_5,
  output [7:0] z_row_6,
  output [7:0] z_row_7
);

  wire [7:0] pow_2_1_z_row_0, pow_2_1_z_row_1, pow_2_1_z_row_2, pow_2_1_z_row_3, pow_2_1_z_row_4,
       pow_2_1_z_row_5, pow_2_1_z_row_6, pow_2_1_z_row_7;

  pow_2 pow_2_1 (
    .x_row_0(x_row_0), .x_row_1(x_row_1), .x_row_2(x_row_2), .x_row_3(x_row_3), .x_row_4(x_row_4),
    .x_row_5(x_row_5), .x_row_6(x_row_6), .x_row_7(x_row_7), .z_row_0(pow_2_1_z_row_0),
    .z_row_1(pow_2_1_z_row_1), .z_row_2(pow_2_1_z_row_2), .z_row_3(pow_2_1_z_row_3),
    .z_row_4(pow_2_1_z_row_4), .z_row_5(pow_2_1_z_row_5), .z_row_6(pow_2_1_z_row_6), .z_row_7(pow_2_1_z_row_7));
  DotMatrix #(.inputtype("row"), .matrixcols(8), .matrixrows(8)) dotmatrix_1 (
    .row0(x_row_0), .row1(x_row_1), .row2(x_row_2), .row3(x_row_3), .row4(x_row_4), .row5(x_row_5),
    .row6(x_row_6), .row7(x_row_7));
  DotMatrix #(.inputtype("row"), .matrixcols(8), .matrixrows(8)) dotmatrix_2 (
    .row0(z_row_0), .row1(z_row_1), .row2(z_row_2), .row3(z_row_3), .row4(z_row_4), .row5(z_row_5),
    .row6(z_row_6), .row7(z_row_7));
  matmul matmul_1 (
    .x_row_0(pow_2_1_z_row_0), .x_row_1(pow_2_1_z_row_1), .x_row_2(pow_2_1_z_row_2),
    .x_row_3(pow_2_1_z_row_3), .x_row_4(pow_2_1_z_row_4), .x_row_5(pow_2_1_z_row_5),
    .x_row_6(pow_2_1_z_row_6), .x_row_7(pow_2_1_z_row_7), .y_row_0(x_row_0), .y_row_1(x_row_1),
    .y_row_2(x_row_2), .y_row_3(x_row_3), .y_row_4(x_row_4), .y_row_5(x_row_5), .y_row_6(x_row_6),
    .y_row_7(x_row_7), .z_row_0(z_row_0), .z_row_1(z_row_1), .z_row_2(z_row_2), .z_row_3(z_row_3),
    .z_row_4(z_row_4), .z_row_5(z_row_5), .z_row_6(z_row_6), .z_row_7(z_row_7));
endmodule

module pow_4 (
  input  [7:0] x_row_0,
  input  [7:0] x_row_1,
  input  [7:0] x_row_2,
  input  [7:0] x_row_3,
  input  [7:0] x_row_4,
  input  [7:0] x_row_5,
  input  [7:0] x_row_6,
  input  [7:0] x_row_7,
  output [7:0] z_row_0,
  output [7:0] z_row_1,
  output [7:0] z_row_2,
  output [7:0] z_row_3,
  output [7:0] z_row_4,
  output [7:0] z_row_5,
  output [7:0] z_row_6,
  output [7:0] z_row_7
);

  wire [7:0] pow_2_1_z_row_0, pow_2_1_z_row_1, pow_2_1_z_row_2, pow_2_1_z_row_3, pow_2_1_z_row_4,
       pow_2_1_z_row_5, pow_2_1_z_row_6, pow_2_1_z_row_7;

  pow_2 pow_2_1 (
    .x_row_0(x_row_0), .x_row_1(x_row_1), .x_row_2(x_row_2), .x_row_3(x_row_3), .x_row_4(x_row_4),
    .x_row_5(x_row_5), .x_row_6(x_row_6), .x_row_7(x_row_7), .z_row_0(pow_2_1_z_row_0),
    .z_row_1(pow_2_1_z_row_1), .z_row_2(pow_2_1_z_row_2), .z_row_3(pow_2_1_z_row_3),
    .z_row_4(pow_2_1_z_row_4), .z_row_5(pow_2_1_z_row_5), .z_row_6(pow_2_1_z_row_6), .z_row_7(pow_2_1_z_row_7));
  DotMatrix #(.inputtype("row"), .matrixcols(8), .matrixrows(8)) dotmatrix_1 (
    .row0(x_row_0), .row1(x_row_1), .row2(x_row_2), .row3(x_row_3), .row4(x_row_4), .row5(x_row_5),
    .row6(x_row_6), .row7(x_row_7));
  DotMatrix #(.inputtype("row"), .matrixcols(8), .matrixrows(8)) dotmatrix_2 (
    .row0(z_row_0), .row1(z_row_1), .row2(z_row_2), .row3(z_row_3), .row4(z_row_4), .row5(z_row_5),
    .row6(z_row_6), .row7(z_row_7));
  pow_2 pow_2_2 (
    .x_row_0(pow_2_1_z_row_0), .x_row_1(pow_2_1_z_row_1), .x_row_2(pow_2_1_z_row_2),
    .x_row_3(pow_2_1_z_row_3), .x_row_4(pow_2_1_z_row_4), .x_row_5(pow_2_1_z_row_5),
    .x_row_6(pow_2_1_z_row_6), .x_row_7(pow_2_1_z_row_7), .z_row_0(z_row_0), .z_row_1(z_row_1),
    .z_row_2(z_row_2), .z_row_3(z_row_3), .z_row_4(z_row_4), .z_row_5(z_row_5), .z_row_6(z_row_6),
    .z_row_7(z_row_7));
endmodule

module pow_5 (
  input  [7:0] x_row_0,
  input  [7:0] x_row_1,
  input  [7:0] x_row_2,
  input  [7:0] x_row_3,
  input  [7:0] x_row_4,
  input  [7:0] x_row_5,
  input  [7:0] x_row_6,
  input  [7:0] x_row_7,
  output [7:0] z_row_0,
  output [7:0] z_row_1,
  output [7:0] z_row_2,
  output [7:0] z_row_3,
  output [7:0] z_row_4,
  output [7:0] z_row_5,
  output [7:0] z_row_6,
  output [7:0] z_row_7
);

  wire [7:0] pow_4_1_z_row_0, pow_4_1_z_row_1, pow_4_1_z_row_2, pow_4_1_z_row_3, pow_4_1_z_row_4,
       pow_4_1_z_row_5, pow_4_1_z_row_6, pow_4_1_z_row_7;

  pow_4 pow_4_1 (
    .x_row_0(x_row_0), .x_row_1(x_row_1), .x_row_2(x_row_2), .x_row_3(x_row_3), .x_row_4(x_row_4),
    .x_row_5(x_row_5), .x_row_6(x_row_6), .x_row_7(x_row_7), .z_row_0(pow_4_1_z_row_0),
    .z_row_1(pow_4_1_z_row_1), .z_row_2(pow_4_1_z_row_2), .z_row_3(pow_4_1_z_row_3),
    .z_row_4(pow_4_1_z_row_4), .z_row_5(pow_4_1_z_row_5), .z_row_6(pow_4_1_z_row_6), .z_row_7(pow_4_1_z_row_7));
  DotMatrix #(.inputtype("row"), .matrixcols(8), .matrixrows(8)) dotmatrix_1 (
    .row0(x_row_0), .row1(x_row_1), .row2(x_row_2), .row3(x_row_3), .row4(x_row_4), .row5(x_row_5),
    .row6(x_row_6), .row7(x_row_7));
  DotMatrix #(.inputtype("row"), .matrixcols(8), .matrixrows(8)) dotmatrix_2 (
    .row0(z_row_0), .row1(z_row_1), .row2(z_row_2), .row3(z_row_3), .row4(z_row_4), .row5(z_row_5),
    .row6(z_row_6), .row7(z_row_7));
  matmul matmul_1 (
    .x_row_0(pow_4_1_z_row_0), .x_row_1(pow_4_1_z_row_1), .x_row_2(pow_4_1_z_row_2),
    .x_row_3(pow_4_1_z_row_3), .x_row_4(pow_4_1_z_row_4), .x_row_5(pow_4_1_z_row_5),
    .x_row_6(pow_4_1_z_row_6), .x_row_7(pow_4_1_z_row_7), .y_row_0(x_row_0), .y_row_1(x_row_1),
    .y_row_2(x_row_2), .y_row_3(x_row_3), .y_row_4(x_row_4), .y_row_5(x_row_5), .y_row_6(x_row_6),
    .y_row_7(x_row_7), .z_row_0(z_row_0), .z_row_1(z_row_1), .z_row_2(z_row_2), .z_row_3(z_row_3),
    .z_row_4(z_row_4), .z_row_5(z_row_5), .z_row_6(z_row_6), .z_row_7(z_row_7));
endmodule

module pow_6 (
  input  [7:0] x_row_0,
  input  [7:0] x_row_1,
  input  [7:0] x_row_2,
  input  [7:0] x_row_3,
  input  [7:0] x_row_4,
  input  [7:0] x_row_5,
  input  [7:0] x_row_6,
  input  [7:0] x_row_7,
  output [7:0] z_row_0,
  output [7:0] z_row_1,
  output [7:0] z_row_2,
  output [7:0] z_row_3,
  output [7:0] z_row_4,
  output [7:0] z_row_5,
  output [7:0] z_row_6,
  output [7:0] z_row_7
);

  wire [7:0] pow_3_1_z_row_0, pow_3_1_z_row_1, pow_3_1_z_row_2, pow_3_1_z_row_3, pow_3_1_z_row_4,
       pow_3_1_z_row_5, pow_3_1_z_row_6, pow_3_1_z_row_7;

  pow_3 pow_3_1 (
    .x_row_0(x_row_0), .x_row_1(x_row_1), .x_row_2(x_row_2), .x_row_3(x_row_3), .x_row_4(x_row_4),
    .x_row_5(x_row_5), .x_row_6(x_row_6), .x_row_7(x_row_7), .z_row_0(pow_3_1_z_row_0),
    .z_row_1(pow_3_1_z_row_1), .z_row_2(pow_3_1_z_row_2), .z_row_3(pow_3_1_z_row_3),
    .z_row_4(pow_3_1_z_row_4), .z_row_5(pow_3_1_z_row_5), .z_row_6(pow_3_1_z_row_6), .z_row_7(pow_3_1_z_row_7));
  DotMatrix #(.inputtype("row"), .matrixcols(8), .matrixrows(8)) dotmatrix_1 (
    .row0(x_row_0), .row1(x_row_1), .row2(x_row_2), .row3(x_row_3), .row4(x_row_4), .row5(x_row_5),
    .row6(x_row_6), .row7(x_row_7));
  DotMatrix #(.inputtype("row"), .matrixcols(8), .matrixrows(8)) dotmatrix_2 (
    .row0(z_row_0), .row1(z_row_1), .row2(z_row_2), .row3(z_row_3), .row4(z_row_4), .row5(z_row_5),
    .row6(z_row_6), .row7(z_row_7));
  pow_2 pow_2_1 (
    .x_row_0(pow_3_1_z_row_0), .x_row_1(pow_3_1_z_row_1), .x_row_2(pow_3_1_z_row_2),
    .x_row_3(pow_3_1_z_row_3), .x_row_4(pow_3_1_z_row_4), .x_row_5(pow_3_1_z_row_5),
    .x_row_6(pow_3_1_z_row_6), .x_row_7(pow_3_1_z_row_7), .z_row_0(z_row_0), .z_row_1(z_row_1),
    .z_row_2(z_row_2), .z_row_3(z_row_3), .z_row_4(z_row_4), .z_row_5(z_row_5), .z_row_6(z_row_6),
    .z_row_7(z_row_7));
endmodule

module pow_7 (
  input  [7:0] x_row_0,
  input  [7:0] x_row_1,
  input  [7:0] x_row_2,
  input  [7:0] x_row_3,
  input  [7:0] x_row_4,
  input  [7:0] x_row_5,
  input  [7:0] x_row_6,
  input  [7:0] x_row_7,
  output [7:0] z_row_0,
  output [7:0] z_row_1,
  output [7:0] z_row_2,
  output [7:0] z_row_3,
  output [7:0] z_row_4,
  output [7:0] z_row_5,
  output [7:0] z_row_6,
  output [7:0] z_row_7
);

  wire [7:0] pow_6_1_z_row_0, pow_6_1_z_row_1, pow_6_1_z_row_2, pow_6_1_z_row_3, pow_6_1_z_row_4,
       pow_6_1_z_row_5, pow_6_1_z_row_6, pow_6_1_z_row_7;

  pow_6 pow_6_1 (
    .x_row_0(x_row_0), .x_row_1(x_row_1), .x_row_2(x_row_2), .x_row_3(x_row_3), .x_row_4(x_row_4),
    .x_row_5(x_row_5), .x_row_6(x_row_6), .x_row_7(x_row_7), .z_row_0(pow_6_1_z_row_0),
    .z_row_1(pow_6_1_z_row_1), .z_row_2(pow_6_1_z_row_2), .z_row_3(pow_6_1_z_row_3),
    .z_row_4(pow_6_1_z_row_4), .z_row_5(pow_6_1_z_row_5), .z_row_6(pow_6_1_z_row_6), .z_row_7(pow_6_1_z_row_7));
  DotMatrix #(.inputtype("row"), .matrixcols(8), .matrixrows(8)) dotmatrix_1 (
    .row0(x_row_0), .row1(x_row_1), .row2(x_row_2), .row3(x_row_3), .row4(x_row_4), .row5(x_row_5),
    .row6(x_row_6), .row7(x_row_7));
  DotMatrix #(.inputtype("row"), .matrixcols(8), .matrixrows(8)) dotmatrix_2 (
    .row0(z_row_0), .row1(z_row_1), .row2(z_row_2), .row3(z_row_3), .row4(z_row_4), .row5(z_row_5),
    .row6(z_row_6), .row7(z_row_7));
  matmul matmul_1 (
    .x_row_0(pow_6_1_z_row_0), .x_row_1(pow_6_1_z_row_1), .x_row_2(pow_6_1_z_row_2),
    .x_row_3(pow_6_1_z_row_3), .x_row_4(pow_6_1_z_row_4), .x_row_5(pow_6_1_z_row_5),
    .x_row_6(pow_6_1_z_row_6), .x_row_7(pow_6_1_z_row_7), .y_row_0(x_row_0), .y_row_1(x_row_1),
    .y_row_2(x_row_2), .y_row_3(x_row_3), .y_row_4(x_row_4), .y_row_5(x_row_5), .y_row_6(x_row_6),
    .y_row_7(x_row_7), .z_row_0(z_row_0), .z_row_1(z_row_1), .z_row_2(z_row_2), .z_row_3(z_row_3),
    .z_row_4(z_row_4), .z_row_5(z_row_5), .z_row_6(z_row_6), .z_row_7(z_row_7));
endmodule

module path_in_exactly_0 (
  input  [7:0] x_row_0,
  input  [7:0] x_row_1,
  input  [7:0] x_row_2,
  input  [7:0] x_row_3,
  input  [7:0] x_row_4,
  input  [7:0] x_row_5,
  input  [7:0] x_row_6,
  input  [7:0] x_row_7,
  input  [2:0] from,
  input  [2:0] to,
  output path_exists
);

  wire [7:0] multiplexer_1_out, pow_0_1_z_row_0, pow_0_1_z_row_1, pow_0_1_z_row_2, pow_0_1_z_row_3,
       pow_0_1_z_row_4, pow_0_1_z_row_5, pow_0_1_z_row_6, pow_0_1_z_row_7, z_row_0, z_row_1, z_row_2,
       z_row_3, z_row_4, z_row_5, z_row_6, z_row_7;

  pow_0 pow_0_1 (
    .x_row_0(x_row_0), .x_row_1(x_row_1), .x_row_2(x_row_2), .x_row_3(x_row_3), .x_row_4(x_row_4),
    .x_row_5(x_row_5), .x_row_6(x_row_6), .x_row_7(x_row_7), .z_row_0(pow_0_1_z_row_0),
    .z_row_1(pow_0_1_z_row_1), .z_row_2(pow_0_1_z_row_2), .z_row_3(pow_0_1_z_row_3),
    .z_row_4(pow_0_1_z_row_4), .z_row_5(pow_0_1_z_row_5), .z_row_6(pow_0_1_z_row_6), .z_row_7(pow_0_1_z_row_7));
  DotMatrix #(.inputtype("row"), .matrixcols(8), .matrixrows(8)) dotmatrix_1 (
    .row0(x_row_0), .row1(x_row_1), .row2(x_row_2), .row3(x_row_3), .row4(x_row_4), .row5(x_row_5),
    .row6(x_row_6), .row7(x_row_7));
  DotMatrix #(.inputtype("row"), .matrixcols(8), .matrixrows(8)) dotmatrix_2 (
    .row0(z_row_0), .row1(z_row_1), .row2(z_row_2), .row3(z_row_3), .row4(z_row_4), .row5(z_row_5),
    .row6(z_row_6), .row7(z_row_7));
  Multiplexer #(.select(3), .width(8), .enable("false")) multiplexer_1 (
    .in0(pow_0_1_z_row_0), .in1(pow_0_1_z_row_1), .in2(pow_0_1_z_row_2), .in3(pow_0_1_z_row_3),
    .in4(pow_0_1_z_row_4), .in5(pow_0_1_z_row_5), .in6(pow_0_1_z_row_6), .in7(pow_0_1_z_row_7),
    .out(multiplexer_1_out), .sel(from));
  Multiplexer #(.select(3), .enable("false")) multiplexer_2 (
    .in0(multiplexer_1_out[7]), .in1(multiplexer_1_out[6]), .in2(multiplexer_1_out[5]),
    .in3(multiplexer_1_out[4]), .in4(multiplexer_1_out[3]), .in5(multiplexer_1_out[2]),
    .in6(multiplexer_1_out[1]), .in7(multiplexer_1_out[0]), .out(path_exists), .sel(to));
endmodule

module path_in_exactly_1 (
  input  [7:0] x_row_0,
  input  [7:0] x_row_1,
  input  [7:0] x_row_2,
  input  [7:0] x_row_3,
  input  [7:0] x_row_4,
  input  [7:0] x_row_5,
  input  [7:0] x_row_6,
  input  [7:0] x_row_7,
  input  [2:0] from,
  input  [2:0] to,
  output path_exists
);

  wire [7:0] multiplexer_1_out, pow_1_1_z_row_0, pow_1_1_z_row_1, pow_1_1_z_row_2, pow_1_1_z_row_3,
       pow_1_1_z_row_4, pow_1_1_z_row_5, pow_1_1_z_row_6, pow_1_1_z_row_7, z_row_0, z_row_1, z_row_2,
       z_row_3, z_row_4, z_row_5, z_row_6, z_row_7;

  pow_1 pow_1_1 (
    .x_row_0(x_row_0), .x_row_1(x_row_1), .x_row_2(x_row_2), .x_row_3(x_row_3), .x_row_4(x_row_4),
    .x_row_5(x_row_5), .x_row_6(x_row_6), .x_row_7(x_row_7), .z_row_0(pow_1_1_z_row_0),
    .z_row_1(pow_1_1_z_row_1), .z_row_2(pow_1_1_z_row_2), .z_row_3(pow_1_1_z_row_3),
    .z_row_4(pow_1_1_z_row_4), .z_row_5(pow_1_1_z_row_5), .z_row_6(pow_1_1_z_row_6), .z_row_7(pow_1_1_z_row_7));
  DotMatrix #(.inputtype("row"), .matrixcols(8), .matrixrows(8)) dotmatrix_1 (
    .row0(x_row_0), .row1(x_row_1), .row2(x_row_2), .row3(x_row_3), .row4(x_row_4), .row5(x_row_5),
    .row6(x_row_6), .row7(x_row_7));
  DotMatrix #(.inputtype("row"), .matrixcols(8), .matrixrows(8)) dotmatrix_2 (
    .row0(z_row_0), .row1(z_row_1), .row2(z_row_2), .row3(z_row_3), .row4(z_row_4), .row5(z_row_5),
    .row6(z_row_6), .row7(z_row_7));
  Multiplexer #(.select(3), .width(8), .enable("false")) multiplexer_1 (
    .in0(pow_1_1_z_row_0), .in1(pow_1_1_z_row_1), .in2(pow_1_1_z_row_2), .in3(pow_1_1_z_row_3),
    .in4(pow_1_1_z_row_4), .in5(pow_1_1_z_row_5), .in6(pow_1_1_z_row_6), .in7(pow_1_1_z_row_7),
    .out(multiplexer_1_out), .sel(from));
  Multiplexer #(.select(3), .enable("false")) multiplexer_2 (
    .in0(multiplexer_1_out[7]), .in1(multiplexer_1_out[6]), .in2(multiplexer_1_out[5]),
    .in3(multiplexer_1_out[4]), .in4(multiplexer_1_out[3]), .in5(multiplexer_1_out[2]),
    .in6(multiplexer_1_out[1]), .in7(multiplexer_1_out[0]), .out(path_exists), .sel(to));
endmodule

module path_in_exactly_2 (
  input  [7:0] x_row_0,
  input  [7:0] x_row_1,
  input  [7:0] x_row_2,
  input  [7:0] x_row_3,
  input  [7:0] x_row_4,
  input  [7:0] x_row_5,
  input  [7:0] x_row_6,
  input  [7:0] x_row_7,
  input  [2:0] from,
  input  [2:0] to,
  output path_exists
);

  wire [7:0] multiplexer_1_out, pow_2_1_z_row_0, pow_2_1_z_row_1, pow_2_1_z_row_2, pow_2_1_z_row_3,
       pow_2_1_z_row_4, pow_2_1_z_row_5, pow_2_1_z_row_6, pow_2_1_z_row_7, z_row_0, z_row_1, z_row_2,
       z_row_3, z_row_4, z_row_5, z_row_6, z_row_7;

  pow_2 pow_2_1 (
    .x_row_0(x_row_0), .x_row_1(x_row_1), .x_row_2(x_row_2), .x_row_3(x_row_3), .x_row_4(x_row_4),
    .x_row_5(x_row_5), .x_row_6(x_row_6), .x_row_7(x_row_7), .z_row_0(pow_2_1_z_row_0),
    .z_row_1(pow_2_1_z_row_1), .z_row_2(pow_2_1_z_row_2), .z_row_3(pow_2_1_z_row_3),
    .z_row_4(pow_2_1_z_row_4), .z_row_5(pow_2_1_z_row_5), .z_row_6(pow_2_1_z_row_6), .z_row_7(pow_2_1_z_row_7));
  DotMatrix #(.inputtype("row"), .matrixcols(8), .matrixrows(8)) dotmatrix_1 (
    .row0(x_row_0), .row1(x_row_1), .row2(x_row_2), .row3(x_row_3), .row4(x_row_4), .row5(x_row_5),
    .row6(x_row_6), .row7(x_row_7));
  DotMatrix #(.inputtype("row"), .matrixcols(8), .matrixrows(8)) dotmatrix_2 (
    .row0(z_row_0), .row1(z_row_1), .row2(z_row_2), .row3(z_row_3), .row4(z_row_4), .row5(z_row_5),
    .row6(z_row_6), .row7(z_row_7));
  Multiplexer #(.select(3), .width(8), .enable("false")) multiplexer_1 (
    .in0(pow_2_1_z_row_0), .in1(pow_2_1_z_row_1), .in2(pow_2_1_z_row_2), .in3(pow_2_1_z_row_3),
    .in4(pow_2_1_z_row_4), .in5(pow_2_1_z_row_5), .in6(pow_2_1_z_row_6), .in7(pow_2_1_z_row_7),
    .out(multiplexer_1_out), .sel(from));
  Multiplexer #(.select(3), .enable("false")) multiplexer_2 (
    .in0(multiplexer_1_out[7]), .in1(multiplexer_1_out[6]), .in2(multiplexer_1_out[5]),
    .in3(multiplexer_1_out[4]), .in4(multiplexer_1_out[3]), .in5(multiplexer_1_out[2]),
    .in6(multiplexer_1_out[1]), .in7(multiplexer_1_out[0]), .out(path_exists), .sel(to));
endmodule

module path_in_exactly_3 (
  input  [7:0] x_row_0,
  input  [7:0] x_row_1,
  input  [7:0] x_row_2,
  input  [7:0] x_row_3,
  input  [7:0] x_row_4,
  input  [7:0] x_row_5,
  input  [7:0] x_row_6,
  input  [7:0] x_row_7,
  input  [2:0] from,
  input  [2:0] to,
  output path_exists
);

  wire [7:0] multiplexer_1_out, pow_3_1_z_row_0, pow_3_1_z_row_1, pow_3_1_z_row_2, pow_3_1_z_row_3,
       pow_3_1_z_row_4, pow_3_1_z_row_5, pow_3_1_z_row_6, pow_3_1_z_row_7, z_row_0, z_row_1, z_row_2,
       z_row_3, z_row_4, z_row_5, z_row_6, z_row_7;

  pow_3 pow_3_1 (
    .x_row_0(x_row_0), .x_row_1(x_row_1), .x_row_2(x_row_2), .x_row_3(x_row_3), .x_row_4(x_row_4),
    .x_row_5(x_row_5), .x_row_6(x_row_6), .x_row_7(x_row_7), .z_row_0(pow_3_1_z_row_0),
    .z_row_1(pow_3_1_z_row_1), .z_row_2(pow_3_1_z_row_2), .z_row_3(pow_3_1_z_row_3),
    .z_row_4(pow_3_1_z_row_4), .z_row_5(pow_3_1_z_row_5), .z_row_6(pow_3_1_z_row_6), .z_row_7(pow_3_1_z_row_7));
  DotMatrix #(.inputtype("row"), .matrixcols(8), .matrixrows(8)) dotmatrix_1 (
    .row0(x_row_0), .row1(x_row_1), .row2(x_row_2), .row3(x_row_3), .row4(x_row_4), .row5(x_row_5),
    .row6(x_row_6), .row7(x_row_7));
  DotMatrix #(.inputtype("row"), .matrixcols(8), .matrixrows(8)) dotmatrix_2 (
    .row0(z_row_0), .row1(z_row_1), .row2(z_row_2), .row3(z_row_3), .row4(z_row_4), .row5(z_row_5),
    .row6(z_row_6), .row7(z_row_7));
  Multiplexer #(.select(3), .width(8), .enable("false")) multiplexer_1 (
    .in0(pow_3_1_z_row_0), .in1(pow_3_1_z_row_1), .in2(pow_3_1_z_row_2), .in3(pow_3_1_z_row_3),
    .in4(pow_3_1_z_row_4), .in5(pow_3_1_z_row_5), .in6(pow_3_1_z_row_6), .in7(pow_3_1_z_row_7),
    .out(multiplexer_1_out), .sel(from));
  Multiplexer #(.select(3), .enable("false")) multiplexer_2 (
    .in0(multiplexer_1_out[7]), .in1(multiplexer_1_out[6]), .in2(multiplexer_1_out[5]),
    .in3(multiplexer_1_out[4]), .in4(multiplexer_1_out[3]), .in5(multiplexer_1_out[2]),
    .in6(multiplexer_1_out[1]), .in7(multiplexer_1_out[0]), .out(path_exists), .sel(to));
endmodule

module path_in_exactly_4 (
  input  [7:0] x_row_0,
  input  [7:0] x_row_1,
  input  [7:0] x_row_2,
  input  [7:0] x_row_3,
  input  [7:0] x_row_4,
  input  [7:0] x_row_5,
  input  [7:0] x_row_6,
  input  [7:0] x_row_7,
  input  [2:0] from,
  input  [2:0] to,
  output path_exists
);

  wire [7:0] multiplexer_1_out, pow_4_1_z_row_0, pow_4_1_z_row_1, pow_4_1_z_row_2, pow_4_1_z_row_3,
       pow_4_1_z_row_4, pow_4_1_z_row_5, pow_4_1_z_row_6, pow_4_1_z_row_7, z_row_0, z_row_1, z_row_2,
       z_row_3, z_row_4, z_row_5, z_row_6, z_row_7;

  pow_4 pow_4_1 (
    .x_row_0(x_row_0), .x_row_1(x_row_1), .x_row_2(x_row_2), .x_row_3(x_row_3), .x_row_4(x_row_4),
    .x_row_5(x_row_5), .x_row_6(x_row_6), .x_row_7(x_row_7), .z_row_0(pow_4_1_z_row_0),
    .z_row_1(pow_4_1_z_row_1), .z_row_2(pow_4_1_z_row_2), .z_row_3(pow_4_1_z_row_3),
    .z_row_4(pow_4_1_z_row_4), .z_row_5(pow_4_1_z_row_5), .z_row_6(pow_4_1_z_row_6), .z_row_7(pow_4_1_z_row_7));
  DotMatrix #(.inputtype("row"), .matrixcols(8), .matrixrows(8)) dotmatrix_1 (
    .row0(x_row_0), .row1(x_row_1), .row2(x_row_2), .row3(x_row_3), .row4(x_row_4), .row5(x_row_5),
    .row6(x_row_6), .row7(x_row_7));
  DotMatrix #(.inputtype("row"), .matrixcols(8), .matrixrows(8)) dotmatrix_2 (
    .row0(z_row_0), .row1(z_row_1), .row2(z_row_2), .row3(z_row_3), .row4(z_row_4), .row5(z_row_5),
    .row6(z_row_6), .row7(z_row_7));
  Multiplexer #(.select(3), .width(8), .enable("false")) multiplexer_1 (
    .in0(pow_4_1_z_row_0), .in1(pow_4_1_z_row_1), .in2(pow_4_1_z_row_2), .in3(pow_4_1_z_row_3),
    .in4(pow_4_1_z_row_4), .in5(pow_4_1_z_row_5), .in6(pow_4_1_z_row_6), .in7(pow_4_1_z_row_7),
    .out(multiplexer_1_out), .sel(from));
  Multiplexer #(.select(3), .enable("false")) multiplexer_2 (
    .in0(multiplexer_1_out[7]), .in1(multiplexer_1_out[6]), .in2(multiplexer_1_out[5]),
    .in3(multiplexer_1_out[4]), .in4(multiplexer_1_out[3]), .in5(multiplexer_1_out[2]),
    .in6(multiplexer_1_out[1]), .in7(multiplexer_1_out[0]), .out(path_exists), .sel(to));
endmodule

module path_in_exactly_5 (
  input  [7:0] x_row_0,
  input  [7:0] x_row_1,
  input  [7:0] x_row_2,
  input  [7:0] x_row_3,
  input  [7:0] x_row_4,
  input  [7:0] x_row_5,
  input  [7:0] x_row_6,
  input  [7:0] x_row_7,
  input  [2:0] from,
  input  [2:0] to,
  output path_exists
);

  wire [7:0] multiplexer_1_out, pow_5_1_z_row_0, pow_5_1_z_row_1, pow_5_1_z_row_2, pow_5_1_z_row_3,
       pow_5_1_z_row_4, pow_5_1_z_row_5, pow_5_1_z_row_6, pow_5_1_z_row_7, z_row_0, z_row_1, z_row_2,
       z_row_3, z_row_4, z_row_5, z_row_6, z_row_7;

  pow_5 pow_5_1 (
    .x_row_0(x_row_0), .x_row_1(x_row_1), .x_row_2(x_row_2), .x_row_3(x_row_3), .x_row_4(x_row_4),
    .x_row_5(x_row_5), .x_row_6(x_row_6), .x_row_7(x_row_7), .z_row_0(pow_5_1_z_row_0),
    .z_row_1(pow_5_1_z_row_1), .z_row_2(pow_5_1_z_row_2), .z_row_3(pow_5_1_z_row_3),
    .z_row_4(pow_5_1_z_row_4), .z_row_5(pow_5_1_z_row_5), .z_row_6(pow_5_1_z_row_6), .z_row_7(pow_5_1_z_row_7));
  DotMatrix #(.inputtype("row"), .matrixcols(8), .matrixrows(8)) dotmatrix_1 (
    .row0(x_row_0), .row1(x_row_1), .row2(x_row_2), .row3(x_row_3), .row4(x_row_4), .row5(x_row_5),
    .row6(x_row_6), .row7(x_row_7));
  DotMatrix #(.inputtype("row"), .matrixcols(8), .matrixrows(8)) dotmatrix_2 (
    .row0(z_row_0), .row1(z_row_1), .row2(z_row_2), .row3(z_row_3), .row4(z_row_4), .row5(z_row_5),
    .row6(z_row_6), .row7(z_row_7));
  Multiplexer #(.select(3), .width(8), .enable("false")) multiplexer_1 (
    .in0(pow_5_1_z_row_0), .in1(pow_5_1_z_row_1), .in2(pow_5_1_z_row_2), .in3(pow_5_1_z_row_3),
    .in4(pow_5_1_z_row_4), .in5(pow_5_1_z_row_5), .in6(pow_5_1_z_row_6), .in7(pow_5_1_z_row_7),
    .out(multiplexer_1_out), .sel(from));
  Multiplexer #(.select(3), .enable("false")) multiplexer_2 (
    .in0(multiplexer_1_out[7]), .in1(multiplexer_1_out[6]), .in2(multiplexer_1_out[5]),
    .in3(multiplexer_1_out[4]), .in4(multiplexer_1_out[3]), .in5(multiplexer_1_out[2]),
    .in6(multiplexer_1_out[1]), .in7(multiplexer_1_out[0]), .out(path_exists), .sel(to));
endmodule

module path_in_exactly_6 (
  input  [7:0] x_row_0,
  input  [7:0] x_row_1,
  input  [7:0] x_row_2,
  input  [7:0] x_row_3,
  input  [7:0] x_row_4,
  input  [7:0] x_row_5,
  input  [7:0] x_row_6,
  input  [7:0] x_row_7,
  input  [2:0] from,
  input  [2:0] to,
  output path_exists
);

  wire [7:0] multiplexer_1_out, pow_6_1_z_row_0, pow_6_1_z_row_1, pow_6_1_z_row_2, pow_6_1_z_row_3,
       pow_6_1_z_row_4, pow_6_1_z_row_5, pow_6_1_z_row_6, pow_6_1_z_row_7, z_row_0, z_row_1, z_row_2,
       z_row_3, z_row_4, z_row_5, z_row_6, z_row_7;

  pow_6 pow_6_1 (
    .x_row_0(x_row_0), .x_row_1(x_row_1), .x_row_2(x_row_2), .x_row_3(x_row_3), .x_row_4(x_row_4),
    .x_row_5(x_row_5), .x_row_6(x_row_6), .x_row_7(x_row_7), .z_row_0(pow_6_1_z_row_0),
    .z_row_1(pow_6_1_z_row_1), .z_row_2(pow_6_1_z_row_2), .z_row_3(pow_6_1_z_row_3),
    .z_row_4(pow_6_1_z_row_4), .z_row_5(pow_6_1_z_row_5), .z_row_6(pow_6_1_z_row_6), .z_row_7(pow_6_1_z_row_7));
  DotMatrix #(.inputtype("row"), .matrixcols(8), .matrixrows(8)) dotmatrix_1 (
    .row0(x_row_0), .row1(x_row_1), .row2(x_row_2), .row3(x_row_3), .row4(x_row_4), .row5(x_row_5),
    .row6(x_row_6), .row7(x_row_7));
  DotMatrix #(.inputtype("row"), .matrixcols(8), .matrixrows(8)) dotmatrix_2 (
    .row0(z_row_0), .row1(z_row_1), .row2(z_row_2), .row3(z_row_3), .row4(z_row_4), .row5(z_row_5),
    .row6(z_row_6), .row7(z_row_7));
  Multiplexer #(.select(3), .width(8), .enable("false")) multiplexer_1 (
    .in0(pow_6_1_z_row_0), .in1(pow_6_1_z_row_1), .in2(pow_6_1_z_row_2), .in3(pow_6_1_z_row_3),
    .in4(pow_6_1_z_row_4), .in5(pow_6_1_z_row_5), .in6(pow_6_1_z_row_6), .in7(pow_6_1_z_row_7),
    .out(multiplexer_1_out), .sel(from));
  Multiplexer #(.select(3), .enable("false")) multiplexer_2 (
    .in0(multiplexer_1_out[7]), .in1(multiplexer_1_out[6]), .in2(multiplexer_1_out[5]),
    .in3(multiplexer_1_out[4]), .in4(multiplexer_1_out[3]), .in5(multiplexer_1_out[2]),
    .in6(multiplexer_1_out[1]), .in7(multiplexer_1_out[0]), .out(path_exists), .sel(to));
endmodule

module path_in_exactly_7 (
  input  [7:0] x_row_0,
  input  [7:0] x_row_1,
  input  [7:0] x_row_2,
  input  [7:0] x_row_3,
  input  [7:0] x_row_4,
  input  [7:0] x_row_5,
  input  [7:0] x_row_6,
  input  [7:0] x_row_7,
  input  [2:0] from,
  input  [2:0] to,
  output path_exists
);

  wire [7:0] multiplexer_1_out, pow_7_1_z_row_0, pow_7_1_z_row_1, pow_7_1_z_row_2, pow_7_1_z_row_3,
       pow_7_1_z_row_4, pow_7_1_z_row_5, pow_7_1_z_row_6, pow_7_1_z_row_7, z_row_0, z_row_1, z_row_2,
       z_row_3, z_row_4, z_row_5, z_row_6, z_row_7;

  pow_7 pow_7_1 (
    .x_row_0(x_row_0), .z_row_0(pow_7_1_z_row_0), .x_row_1(x_row_1), .z_row_1(pow_7_1_z_row_1),
    .x_row_2(x_row_2), .z_row_2(pow_7_1_z_row_2), .x_row_3(x_row_3), .z_row_3(pow_7_1_z_row_3),
    .x_row_4(x_row_4), .z_row_4(pow_7_1_z_row_4), .x_row_5(x_row_5), .z_row_5(pow_7_1_z_row_5),
    .x_row_6(x_row_6), .z_row_6(pow_7_1_z_row_6), .x_row_7(x_row_7), .z_row_7(pow_7_1_z_row_7));
  DotMatrix #(.inputtype("row"), .matrixcols(8), .matrixrows(8)) dotmatrix_1 (
    .row0(x_row_0), .row1(x_row_1), .row2(x_row_2), .row3(x_row_3), .row4(x_row_4), .row5(x_row_5),
    .row6(x_row_6), .row7(x_row_7));
  DotMatrix #(.inputtype("row"), .matrixcols(8), .matrixrows(8)) dotmatrix_2 (
    .row0(z_row_0), .row1(z_row_1), .row2(z_row_2), .row3(z_row_3), .row4(z_row_4), .row5(z_row_5),
    .row6(z_row_6), .row7(z_row_7));
  Multiplexer #(.select(3), .width(8), .enable("false")) multiplexer_1 (
    .in0(pow_7_1_z_row_0), .in1(pow_7_1_z_row_1), .in2(pow_7_1_z_row_2), .in3(pow_7_1_z_row_3),
    .in4(pow_7_1_z_row_4), .in5(pow_7_1_z_row_5), .in6(pow_7_1_z_row_6), .in7(pow_7_1_z_row_7),
    .out(multiplexer_1_out), .sel(from));
  Multiplexer #(.select(3), .enable("false")) multiplexer_2 (
    .in0(multiplexer_1_out[7]), .in1(multiplexer_1_out[6]), .in2(multiplexer_1_out[5]),
    .in3(multiplexer_1_out[4]), .in4(multiplexer_1_out[3]), .in5(multiplexer_1_out[2]),
    .in6(multiplexer_1_out[1]), .in7(multiplexer_1_out[0]), .out(path_exists), .sel(to));
endmodule

module min_dist_i_j (
  input  [7:0] x_row_0,
  input  [7:0] x_row_1,
  input  [7:0] x_row_2,
  input  [7:0] x_row_3,
  input  [7:0] x_row_4,
  input  [7:0] x_row_5,
  input  [7:0] x_row_6,
  input  [7:0] x_row_7,
  input  [2:0] from,
  input  [2:0] to,
  output path_exists,
  output [2:0] min_dist
);

  wire L_0, L_1, L_2, L_3, L_4, L_5, L_6, L_7, or_1_out, or_2_out, or_3_out, or_4_out, or_5_out, or_6_out;
  wire [2:0] multiplexer_1_out, multiplexer_2_out, multiplexer_3_out, multiplexer_4_out, multiplexer_5_out,
       multiplexer_6_out, multiplexer_7_out, undriven;

  Multiplexer #(.width(3), .enable("false")) multiplexer_1 (
    .in0(undriven), .in1(3'b111), .out(multiplexer_1_out), .sel(L_7));
  Multiplexer #(.width(3), .enable("false")) multiplexer_2 (
    .in0(multiplexer_1_out), .in1(3'b110), .out(multiplexer_2_out), .sel(L_6));
  Multiplexer #(.width(3), .enable("false")) multiplexer_3 (
    .in0(multiplexer_2_out), .in1(3'b101), .out(multiplexer_3_out), .sel(L_5));
  path_in_exactly_0 path_in_exactly_0_1 (
    .x_row_0(x_row_0), .x_row_1(x_row_1), .x_row_2(x_row_2), .x_row_3(x_row_3), .x_row_4(x_row_4),
    .x_row_5(x_row_5), .x_row_6(x_row_6), .x_row_7(x_row_7), .from(from), .to(to), .path_exists(L_0));
  path_in_exactly_1 path_in_exactly_1_1 (
    .x_row_0(x_row_0), .x_row_1(x_row_1), .x_row_2(x_row_2), .x_row_3(x_row_3), .x_row_4(x_row_4),
    .x_row_5(x_row_5), .x_row_6(x_row_6), .x_row_7(x_row_7), .from(from), .to(to), .path_exists(L_1));
  path_in_exactly_2 path_in_exactly_2_1 (
    .x_row_0(x_row_0), .x_row_1(x_row_1), .x_row_2(x_row_2), .x_row_3(x_row_3), .x_row_4(x_row_4),
    .x_row_5(x_row_5), .x_row_6(x_row_6), .x_row_7(x_row_7), .from(from), .to(to), .path_exists(L_2));
  path_in_exactly_3 path_in_exactly_3_1 (
    .x_row_0(x_row_0), .x_row_1(x_row_1), .x_row_2(x_row_2), .x_row_3(x_row_3), .x_row_4(x_row_4),
    .x_row_5(x_row_5), .x_row_6(x_row_6), .x_row_7(x_row_7), .from(from), .to(to), .path_exists(L_3));
  Multiplexer #(.width(3), .enable("false")) multiplexer_4 (
    .in0(multiplexer_3_out), .in1(3'b100), .out(multiplexer_4_out), .sel(L_4));
  Multiplexer #(.width(3), .enable("false")) multiplexer_5 (
    .in0(multiplexer_4_out), .in1(3'b011), .out(multiplexer_5_out), .sel(L_3));
  Multiplexer #(.width(3), .enable("false")) multiplexer_6 (
    .in0(multiplexer_5_out), .in1(3'b010), .out(multiplexer_6_out), .sel(L_2));
  Multiplexer #(.width(3), .enable("false")) multiplexer_7 (
    .in0(multiplexer_6_out), .in1(3'b001), .out(multiplexer_7_out), .sel(L_1));
  Multiplexer #(.width(3), .enable("false")) multiplexer_8 (
    .in0(multiplexer_7_out), .in1(3'b000), .out(min_dist), .sel(L_0));
  path_in_exactly_4 path_in_exactly_4_1 (
    .x_row_0(x_row_0), .x_row_1(x_row_1), .x_row_2(x_row_2), .x_row_3(x_row_3), .x_row_4(x_row_4),
    .x_row_5(x_row_5), .x_row_6(x_row_6), .x_row_7(x_row_7), .from(from), .to(to), .path_exists(L_4));
  path_in_exactly_5 path_in_exactly_5_1 (
    .x_row_0(x_row_0), .x_row_1(x_row_1), .x_row_2(x_row_2), .x_row_3(x_row_3), .x_row_4(x_row_4),
    .x_row_5(x_row_5), .x_row_6(x_row_6), .x_row_7(x_row_7), .from(from), .to(to), .path_exists(L_5));
  path_in_exactly_6 path_in_exactly_6_1 (
    .x_row_0(x_row_0), .x_row_1(x_row_1), .x_row_2(x_row_2), .x_row_3(x_row_3), .x_row_4(x_row_4),
    .x_row_5(x_row_5), .x_row_6(x_row_6), .x_row_7(x_row_7), .from(from), .to(to), .path_exists(L_6));
  path_in_exactly_7 path_in_exactly_7_1 (
    .x_row_0(x_row_0), .x_row_1(x_row_1), .x_row_2(x_row_2), .x_row_3(x_row_3), .x_row_4(x_row_4),
    .x_row_5(x_row_5), .x_row_6(x_row_6), .x_row_7(x_row_7), .from(from), .to(to), .path_exists(L_7));
  or or_1 (or_1_out, L_0, L_1);
  or or_2 (or_2_out, L_2, L_3);
  or or_3 (or_3_out, L_4, L_5);
  or or_4 (or_4_out, L_6, L_7);
  or or_5 (or_5_out, or_1_out, or_2_out);
  or or_6 (or_6_out, or_3_out, or_4_out);
  or or_7 (path_exists, or_5_out, or_6_out);
  // Probe on min_dist
endmodule

module matrix_and_8_8 (
  input  [7:0] x_row_0,
  input  [7:0] x_row_1,
  input  [7:0] x_row_2,
  input  [7:0] x_row_3,
  input  [7:0] x_row_4,
  input  [7:0] x_row_5,
  input  [7:0] x_row_6,
  input  [7:0] x_row_7,
  output z
);

  wire [1:0] and_9_out;
  wire [3:0] and_8_out;
  wire [7:0] and_1_out, and_2_out, and_3_out, and_4_out, and_5_out, and_6_out, and_7_out, z_row_0, z_row_1,
       z_row_2, z_row_3, z_row_4, z_row_5, z_row_6, z_row_7;

  assign and_1_out = x_row_0 & x_row_1;  // AND_Gate and_1, 8 bits wide
  assign and_2_out = x_row_2 & x_row_3;  // AND_Gate and_2, 8 bits wide
  assign and_3_out = x_row_4 & x_row_5;  // AND_Gate and_3, 8 bits wide
  assign and_4_out = x_row_6 & x_row_7;  // AND_Gate and_4, 8 bits wide
  DotMatrix #(.inputtype("row"), .matrixcols(8), .matrixrows(8)) dotmatrix_1 (
    .row0(x_row_0), .row1(x_row_1), .row2(x_row_2), .row3(x_row_3), .row4(x_row_4), .row5(x_row_5),
    .row6(x_row_6), .row7(x_row_7));
  assign and_5_out = and_1_out & and_2_out;  // AND_Gate and_5, 8 bits wide
  assign and_6_out = and_3_out & and_4_out;  // AND_Gate and_6, 8 bits wide
  assign and_7_out = and_5_out & and_6_out;  // AND_Gate and_7, 8 bits wide
  assign and_8_out = and_7_out[3:0] & and_7_out[7:4];  // AND_Gate and_8, 4 bits wide
  assign and_9_out = and_8_out[1:0] & and_8_out[3:2];  // AND_Gate and_9, 2 bits wide
  and and_10 (z, and_9_out[0], and_9_out[1]);
  DotMatrix #(.inputtype("row"), .matrixcols(8), .matrixrows(8)) dotmatrix_2 (
    .row0(z_row_0), .row1(z_row_1), .row2(z_row_2), .row3(z_row_3), .row4(z_row_4), .row5(z_row_5),
    .row6(z_row_6), .row7(z_row_7));
endmodule

module min_dist_anywhere (
  input  [7:0] x_row_0,
  input  [7:0] x_row_1,
  input  [7:0] x_row_2,
  input  [7:0] x_row_3,
  input  [7:0] x_row_4,
  input  [7:0] x_row_5,
  input  [7:0] x_row_6,
  input  [7:0] x_row_7,
  output path_exists,
  output [2:0] min_dist
);

  wire L_0, L_1, L_2, L_3, L_4, L_5, L_6, L_7, or_1_out, or_2_out, or_3_out, or_4_out, or_5_out, or_7_out;
  wire [2:0] multiplexer_1_out, multiplexer_2_out, multiplexer_3_out, multiplexer_4_out, multiplexer_5_out,
       multiplexer_6_out, multiplexer_7_out, undriven;
  wire [7:0] pow_0_1_z_row_0, pow_0_1_z_row_1, pow_0_1_z_row_2, pow_0_1_z_row_3, pow_0_1_z_row_4,
       pow_0_1_z_row_5, pow_0_1_z_row_6, pow_0_1_z_row_7, pow_1_1_z_row_0, pow_1_1_z_row_1, pow_1_1_z_row_2,
       pow_1_1_z_row_3, pow_1_1_z_row_4, pow_1_1_z_row_5, pow_1_1_z_row_6, pow_1_1_z_row_7, pow_2_1_z_row_0,
       pow_2_1_z_row_1, pow_2_1_z_row_2, pow_2_1_z_row_3, pow_2_1_z_row_4, pow_2_1_z_row_5, pow_2_1_z_row_6,
       pow_2_1_z_row_7, pow_3_1_z_row_0, pow_3_1_z_row_1, pow_3_1_z_row_2, pow_3_1_z_row_3, pow_3_1_z_row_4,
       pow_3_1_z_row_5, pow_3_1_z_row_6, pow_3_1_z_row_7, pow_4_1_z_row_0, pow_4_1_z_row_1, pow_4_1_z_row_2,
       pow_4_1_z_row_3, pow_4_1_z_row_4, pow_4_1_z_row_5, pow_4_1_z_row_6, pow_4_1_z_row_7, pow_5_1_z_row_0,
       pow_5_1_z_row_1, pow_5_1_z_row_2, pow_5_1_z_row_3, pow_5_1_z_row_4, pow_5_1_z_row_5, pow_5_1_z_row_6,
       pow_5_1_z_row_7, pow_6_1_z_row_0, pow_6_1_z_row_1, pow_6_1_z_row_2, pow_6_1_z_row_3, pow_6_1_z_row_4,
       pow_6_1_z_row_5, pow_6_1_z_row_6, pow_6_1_z_row_7, pow_7_1_z_row_0, pow_7_1_z_row_1, pow_7_1_z_row_2,
       pow_7_1_z_row_3, pow_7_1_z_row_4, pow_7_1_z_row_5, pow_7_1_z_row_6, pow_7_1_z_row_7;

  Multiplexer #(.width(3), .enable("false")) multiplexer_1 (
    .in0(undriven), .in1(3'b111), .out(multiplexer_1_out), .sel(L_7));
  Multiplexer #(.width(3), .enable("false")) multiplexer_2 (
    .in0(multiplexer_1_out), .in1(3'b110), .out(multiplexer_2_out), .sel(L_6));
  Multiplexer #(.width(3), .enable("false")) multiplexer_3 (
    .in0(multiplexer_2_out), .in1(3'b101), .out(multiplexer_3_out), .sel(L_5));
  pow_0 pow_0_1 (
    .x_row_0(x_row_0), .x_row_1(x_row_1), .x_row_2(x_row_2), .x_row_3(x_row_3), .x_row_4(x_row_4),
    .x_row_5(x_row_5), .x_row_6(x_row_6), .x_row_7(x_row_7), .z_row_0(pow_0_1_z_row_0),
    .z_row_1(pow_0_1_z_row_1), .z_row_2(pow_0_1_z_row_2), .z_row_3(pow_0_1_z_row_3),
    .z_row_4(pow_0_1_z_row_4), .z_row_5(pow_0_1_z_row_5), .z_row_6(pow_0_1_z_row_6), .z_row_7(pow_0_1_z_row_7));
  pow_1 pow_1_1 (
    .x_row_0(x_row_0), .x_row_1(x_row_1), .x_row_2(x_row_2), .x_row_3(x_row_3), .x_row_4(x_row_4),
    .x_row_5(x_row_5), .x_row_6(x_row_6), .x_row_7(x_row_7), .z_row_0(pow_1_1_z_row_0),
    .z_row_1(pow_1_1_z_row_1), .z_row_2(pow_1_1_z_row_2), .z_row_3(pow_1_1_z_row_3),
    .z_row_4(pow_1_1_z_row_4), .z_row_5(pow_1_1_z_row_5), .z_row_6(pow_1_1_z_row_6), .z_row_7(pow_1_1_z_row_7));
  pow_2 pow_2_1 (
    .x_row_0(x_row_0), .x_row_1(x_row_1), .x_row_2(x_row_2), .x_row_3(x_row_3), .x_row_4(x_row_4),
    .x_row_5(x_row_5), .x_row_6(x_row_6), .x_row_7(x_row_7), .z_row_0(pow_2_1_z_row_0),
    .z_row_1(pow_2_1_z_row_1), .z_row_2(pow_2_1_z_row_2), .z_row_3(pow_2_1_z_row_3),
    .z_row_4(pow_2_1_z_row_4), .z_row_5(pow_2_1_z_row_5), .z_row_6(pow_2_1_z_row_6), .z_row_7(pow_2_1_z_row_7));
  pow_3 pow_3_1 (
    .x_row_0(x_row_0), .x_row_1(x_row_1), .x_row_2(x_row_2), .x_row_3(x_row_3), .x_row_4(x_row_4),
    .x_row_5(x_row_5), .x_row_6(x_row_6), .x_row_7(x_row_7), .z_row_0(pow_3_1_z_row_0),
    .z_row_1(pow_3_1_z_row_1), .z_row_2(pow_3_1_z_row_2), .z_row_3(pow_3_1_z_row_3),
    .z_row_4(pow_3_1_z_row_4), .z_row_5(pow_3_1_z_row_5), .z_row_6(pow_3_1_z_row_6), .z_row_7(pow_3_1_z_row_7));
  Multiplexer #(.width(3), .enable("false")) multiplexer_4 (
    .in0(multiplexer_3_out), .in1(3'b100), .out(multiplexer_4_out), .sel(L_4));
  matrix_and_8_8 matrix_and_8_8_1 (
    .x_row_0(pow_0_1_z_row_0), .x_row_1(pow_0_1_z_row_1), .x_row_2(pow_0_1_z_row_2),
    .x_row_3(pow_0_1_z_row_3), .x_row_4(pow_0_1_z_row_4), .x_row_5(pow_0_1_z_row_5),
    .x_row_6(pow_0_1_z_row_6), .x_row_7(pow_0_1_z_row_7), .z(L_0));
  matrix_and_8_8 matrix_and_8_8_2 (
    .x_row_0(pow_1_1_z_row_0), .x_row_1(pow_1_1_z_row_1), .x_row_2(pow_1_1_z_row_2),
    .x_row_3(pow_1_1_z_row_3), .x_row_4(pow_1_1_z_row_4), .x_row_5(pow_1_1_z_row_5),
    .x_row_6(pow_1_1_z_row_6), .x_row_7(pow_1_1_z_row_7), .z(L_1));
  matrix_and_8_8 matrix_and_8_8_3 (
    .x_row_0(pow_2_1_z_row_0), .x_row_1(pow_2_1_z_row_1), .x_row_2(pow_2_1_z_row_2),
    .x_row_3(pow_2_1_z_row_3), .x_row_4(pow_2_1_z_row_4), .x_row_5(pow_2_1_z_row_5),
    .x_row_6(pow_2_1_z_row_6), .x_row_7(pow_2_1_z_row_7), .z(L_2));
  matrix_and_8_8 matrix_and_8_8_4 (
    .x_row_0(pow_3_1_z_row_0), .x_row_1(pow_3_1_z_row_1), .x_row_2(pow_3_1_z_row_2),
    .x_row_3(pow_3_1_z_row_3), .x_row_4(pow_3_1_z_row_4), .x_row_5(pow_3_1_z_row_5),
    .x_row_6(pow_3_1_z_row_6), .x_row_7(pow_3_1_z_row_7), .z(L_3));
  Multiplexer #(.width(3), .enable("false")) multiplexer_5 (
    .in0(multiplexer_4_out), .in1(3'b011), .out(multiplexer_5_out), .sel(L_3));
  Multiplexer #(.width(3), .enable("false")) multiplexer_6 (
    .in0(multiplexer_5_out), .in1(3'b010), .out(multiplexer_6_out), .sel(L_2));
  Multiplexer #(.width(3), .enable("false")) multiplexer_7 (
    .in0(multiplexer_6_out), .in1(3'b001), .out(multiplexer_7_out), .sel(L_1));
  Multiplexer #(.width(3), .enable("false")) multiplexer_8 (
    .in0(multiplexer_7_out), .in1(3'b000), .out(min_dist), .sel(L_0));
  pow_4 pow_4_1 (
    .x_row_0(x_row_0), .x_row_1(x_row_1), .x_row_2(x_row_2), .x_row_3(x_row_3), .x_row_4(x_row_4),
    .x_row_5(x_row_5), .x_row_6(x_row_6), .x_row_7(x_row_7), .z_row_0(pow_4_1_z_row_0),
    .z_row_1(pow_4_1_z_row_1), .z_row_2(pow_4_1_z_row_2), .z_row_3(pow_4_1_z_row_3),
    .z_row_4(pow_4_1_z_row_4), .z_row_5(pow_4_1_z_row_5), .z_row_6(pow_4_1_z_row_6), .z_row_7(pow_4_1_z_row_7));
  pow_5 pow_5_1 (
    .x_row_0(x_row_0), .x_row_1(x_row_1), .x_row_2(x_row_2), .x_row_3(x_row_3), .x_row_4(x_row_4),
    .x_row_5(x_row_5), .x_row_6(x_row_6), .x_row_7(x_row_7), .z_row_0(pow_5_1_z_row_0),
    .z_row_1(pow_5_1_z_row_1), .z_row_2(pow_5_1_z_row_2), .z_row_3(pow_5_1_z_row_3),
    .z_row_4(pow_5_1_z_row_4), .z_row_5(pow_5_1_z_row_5), .z_row_6(pow_5_1_z_row_6), .z_row_7(pow_5_1_z_row_7));
  pow_6 pow_6_1 (
    .x_row_0(x_row_0), .x_row_1(x_row_1), .x_row_2(x_row_2), .x_row_3(x_row_3), .x_row_4(x_row_4),
    .x_row_5(x_row_5), .x_row_6(x_row_6), .x_row_7(x_row_7), .z_row_0(pow_6_1_z_row_0),
    .z_row_1(pow_6_1_z_row_1), .z_row_2(pow_6_1_z_row_2), .z_row_3(pow_6_1_z_row_3),
    .z_row_4(pow_6_1_z_row_4), .z_row_5(pow_6_1_z_row_5), .z_row_6(pow_6_1_z_row_6), .z_row_7(pow_6_1_z_row_7));
  pow_7 pow_7_1 (
    .x_row_0(x_row_0), .z_row_0(pow_7_1_z_row_0), .x_row_1(x_row_1), .z_row_1(pow_7_1_z_row_1),
    .x_row_2(x_row_2), .z_row_2(pow_7_1_z_row_2), .x_row_3(x_row_3), .z_row_3(pow_7_1_z_row_3),
    .x_row_4(x_row_4), .z_row_4(pow_7_1_z_row_4), .x_row_5(x_row_5), .z_row_5(pow_7_1_z_row_5),
    .x_row_6(x_row_6), .z_row_6(pow_7_1_z_row_6), .x_row_7(x_row_7), .z_row_7(pow_7_1_z_row_7));
  matrix_and_8_8 matrix_and_8_8_5 (
    .x_row_0(pow_4_1_z_row_0), .x_row_1(pow_4_1_z_row_1), .x_row_2(pow_4_1_z_row_2),
    .x_row_3(pow_4_1_z_row_3), .x_row_4(pow_4_1_z_row_4), .x_row_5(pow_4_1_z_row_5),
    .x_row_6(pow_4_1_z_row_6), .x_row_7(pow_4_1_z_row_7), .z(L_4));
  matrix_and_8_8 matrix_and_8_8_6 (
    .x_row_0(pow_5_1_z_row_0), .x_row_1(pow_5_1_z_row_1), .x_row_2(pow_5_1_z_row_2),
    .x_row_3(pow_5_1_z_row_3), .x_row_4(pow_5_1_z_row_4), .x_row_5(pow_5_1_z_row_5),
    .x_row_6(pow_5_1_z_row_6), .x_row_7(pow_5_1_z_row_7), .z(L_5));
  matrix_and_8_8 matrix_and_8_8_7 (
    .x_row_0(pow_6_1_z_row_0), .x_row_1(pow_6_1_z_row_1), .x_row_2(pow_6_1_z_row_2),
    .x_row_3(pow_6_1_z_row_3), .x_row_4(pow_6_1_z_row_4), .x_row_5(pow_6_1_z_row_5),
    .x_row_6(pow_6_1_z_row_6), .x_row_7(pow_6_1_z_row_7), .z(L_6));
  matrix_and_8_8 matrix_and_8_8_8 (
    .x_row_0(pow_7_1_z_row_0), .x_row_1(pow_7_1_z_row_1), .x_row_2(pow_7_1_z_row_2),
    .x_row_3(pow_7_1_z_row_3), .x_row_4(pow_7_1_z_row_4), .x_row_5(pow_7_1_z_row_5),
    .x_row_6(pow_7_1_z_row_6), .x_row_7(pow_7_1_z_row_7), .z(L_7));
  // Probe on min_dist
  or or_1 (or_1_out, L_0, L_1);
  or or_2 (or_2_out, L_2, L_3);
  or or_3 (or_3_out, L_4, L_5);
  or or_4 (or_4_out, L_6, L_7);
  or or_5 (or_5_out, or_1_out, or_2_out);
  or or_6 (path_exists, or_5_out, or_7_out);
  or or_7 (or_7_out, or_3_out, or_4_out);
endmodule

module exactly (
  input  [7:0] x_row_0,
  input  [7:0] x_row_1,
  input  [7:0] x_row_2,
  input  [7:0] x_row_3,
  input  [7:0] x_row_4,
  input  [7:0] x_row_5,
  input  [7:0] x_row_6,
  input  [7:0] x_row_7,
  input  [2:0] from,
  input  [2:0] to,
  input  [2:0] num_steps,
  output path_exists
);

  wire L_0, L_1, L_2, L_3, L_4, L_5, L_6, L_7;

  DotMatrix #(.inputtype("row"), .matrixcols(8), .matrixrows(8)) dotmatrix_1 (
    .row0(x_row_0), .row1(x_row_1), .row2(x_row_2), .row3(x_row_3), .row4(x_row_4), .row5(x_row_5),
    .row6(x_row_6), .row7(x_row_7));
  path_in_exactly_0 path_in_exactly_0_1 (
    .x_row_0(x_row_0), .x_row_1(x_row_1), .x_row_2(x_row_2), .x_row_3(x_row_3), .x_row_4(x_row_4),
    .x_row_5(x_row_5), .x_row_6(x_row_6), .x_row_7(x_row_7), .from(from), .to(to), .path_exists(L_0));
  path_in_exactly_1 path_in_exactly_1_1 (
    .x_row_0(x_row_0), .x_row_1(x_row_1), .x_row_2(x_row_2), .x_row_3(x_row_3), .x_row_4(x_row_4),
    .x_row_5(x_row_5), .x_row_6(x_row_6), .x_row_7(x_row_7), .from(from), .to(to), .path_exists(L_1));
  path_in_exactly_2 path_in_exactly_2_1 (
    .x_row_0(x_row_0), .x_row_1(x_row_1), .x_row_2(x_row_2), .x_row_3(x_row_3), .x_row_4(x_row_4),
    .x_row_5(x_row_5), .x_row_6(x_row_6), .x_row_7(x_row_7), .from(from), .to(to), .path_exists(L_2));
  path_in_exactly_3 path_in_exactly_3_1 (
    .x_row_0(x_row_0), .x_row_1(x_row_1), .x_row_2(x_row_2), .x_row_3(x_row_3), .x_row_4(x_row_4),
    .x_row_5(x_row_5), .x_row_6(x_row_6), .x_row_7(x_row_7), .from(from), .to(to), .path_exists(L_3));
  path_in_exactly_4 path_in_exactly_4_1 (
    .x_row_0(x_row_0), .x_row_1(x_row_1), .x_row_2(x_row_2), .x_row_3(x_row_3), .x_row_4(x_row_4),
    .x_row_5(x_row_5), .x_row_6(x_row_6), .x_row_7(x_row_7), .from(from), .to(to), .path_exists(L_4));
  path_in_exactly_5 path_in_exactly_5_1 (
    .x_row_0(x_row_0), .x_row_1(x_row_1), .x_row_2(x_row_2), .x_row_3(x_row_3), .x_row_4(x_row_4),
    .x_row_5(x_row_5), .x_row_6(x_row_6), .x_row_7(x_row_7), .from(from), .to(to), .path_exists(L_5));
  path_in_exactly_6 path_in_exactly_6_1 (
    .x_row_0(x_row_0), .x_row_1(x_row_1), .x_row_2(x_row_2), .x_row_3(x_row_3), .x_row_4(x_row_4),
    .x_row_5(x_row_5), .x_row_6(x_row_6), .x_row_7(x_row_7), .from(from), .to(to), .path_exists(L_6));
  path_in_exactly_7 path_in_exactly_7_1 (
    .x_row_0(x_row_0), .x_row_1(x_row_1), .x_row_2(x_row_2), .x_row_3(x_row_3), .x_row_4(x_row_4),
    .x_row_5(x_row_5), .x_row_6(x_row_6), .x_row_7(x_row_7), .from(from), .to(to), .path_exists(L_7));
  Multiplexer #(.select(3), .enable("false")) multiplexer_1 (
    .in0(L_0), .in1(L_1), .in2(L_2), .in3(L_3), .in4(L_4), .in5(L_5), .in6(L_6), .in7(L_7),
    .out(path_exists), .sel(num_steps));
endmodule

module atmost (
  input  [7:0] x_row_0,
  input  [7:0] x_row_1,
  input  [7:0] x_row_2,
  input  [7:0] x_row_3,
  input  [7:0] x_row_4,
  input  [7:0] x_row_5,
  input  [7:0] x_row_6,
  input  [7:0] x_row_7,
  input  [2:0] from,
  input  [2:0] to,
  input  [2:0] num_steps,
  output path_exists
);

  wire L_0, L_1, L_2, L_3, L_4, L_5, L_6, L_7, or_1_out, or_2_out, or_3_out, or_4_out, or_5_out, or_6_out,
       or_7_out;

  DotMatrix #(.inputtype("row"), .matrixcols(8), .matrixrows(8)) dotmatrix_1 (
    .row0(x_row_0), .row1(x_row_1), .row2(x_row_2), .row3(x_row_3), .row4(x_row_4), .row5(x_row_5),
    .row6(x_row_6), .row7(x_row_7));
  path_in_exactly_0 path_in_exactly_0_1 (
    .x_row_0(x_row_0), .x_row_1(x_row_1), .x_row_2(x_row_2), .x_row_3(x_row_3), .x_row_4(x_row_4),
    .x_row_5(x_row_5), .x_row_6(x_row_6), .x_row_7(x_row_7), .from(from), .to(to), .path_exists(L_0));
  path_in_exactly_1 path_in_exactly_1_1 (
    .x_row_0(x_row_0), .x_row_1(x_row_1), .x_row_2(x_row_2), .x_row_3(x_row_3), .x_row_4(x_row_4),
    .x_row_5(x_row_5), .x_row_6(x_row_6), .x_row_7(x_row_7), .from(from), .to(to), .path_exists(L_1));
  path_in_exactly_2 path_in_exactly_2_1 (
    .x_row_0(x_row_0), .x_row_1(x_row_1), .x_row_2(x_row_2), .x_row_3(x_row_3), .x_row_4(x_row_4),
    .x_row_5(x_row_5), .x_row_6(x_row_6), .x_row_7(x_row_7), .from(from), .to(to), .path_exists(L_2));
  path_in_exactly_3 path_in_exactly_3_1 (
    .x_row_0(x_row_0), .x_row_1(x_row_1), .x_row_2(x_row_2), .x_row_3(x_row_3), .x_row_4(x_row_4),
    .x_row_5(x_row_5), .x_row_6(x_row_6), .x_row_7(x_row_7), .from(from), .to(to), .path_exists(L_3));
  path_in_exactly_4 path_in_exactly_4_1 (
    .x_row_0(x_row_0), .x_row_1(x_row_1), .x_row_2(x_row_2), .x_row_3(x_row_3), .x_row_4(x_row_4),
    .x_row_5(x_row_5), .x_row_6(x_row_6), .x_row_7(x_row_7), .from(from), .to(to), .path_exists(L_4));
  path_in_exactly_5 path_in_exactly_5_1 (
    .x_row_0(x_row_0), .x_row_1(x_row_1), .x_row_2(x_row_2), .x_row_3(x_row_3), .x_row_4(x_row_4),
    .x_row_5(x_row_5), .x_row_6(x_row_6), .x_row_7(x_row_7), .from(from), .to(to), .path_exists(L_5));
  path_in_exactly_6 path_in_exactly_6_1 (
    .x_row_0(x_row_0), .x_row_1(x_row_1), .x_row_2(x_row_2), .x_row_3(x_row_3), .x_row_4(x_row_4),
    .x_row_5(x_row_5), .x_row_6(x_row_6), .x_row_7(x_row_7), .from(from), .to(to), .path_exists(L_6));
  path_in_exactly_7 path_in_exactly_7_1 (
    .x_row_0(x_row_0), .x_row_1(x_row_1), .x_row_2(x_row_2), .x_row_3(x_row_3), .x_row_4(x_row_4),
    .x_row_5(x_row_5), .x_row_6(x_row_6), .x_row_7(x_row_7), .from(from), .to(to), .path_exists(L_7));
  or or_1 (or_1_out, L_0, L_1);
  or or_2 (or_2_out, or_1_out, L_2);
  or or_3 (or_3_out, or_2_out, L_3);
  or or_4 (or_4_out, or_3_out, L_4);
  or or_5 (or_5_out, or_4_out, L_5);
  or or_6 (or_6_out, or_5_out, L_6);
  or or_7 (or_7_out, or_6_out, L_7);
  Multiplexer #(.select(3), .enable("false")) multiplexer_1 (
    .in0(L_0), .in1(or_1_out), .in2(or_2_out), .in3(or_3_out), .in4(or_4_out), .in5(or_5_out),
    .in6(or_6_out), .in7(or_7_out), .out(path_exists), .sel(num_steps));
endmodule
